// Logisim project CdM8_mb5.circ as structural Verilog: 23 circuits, main circuit CdM8_mb5
module CdM8_mb5 (
);

  wire and_1_out, and_2_out, and_3_out, button_5_out, button_6_out, button_7_out, button_8_out, button_9_out,
       button_10_out, button_11_out, button_12_out, cdm_8_mark5_1_data_inst, Clock, comparator_1_eq, Data,
       DOWN_out, I_O, IAck, Inst, IR_Enable, ir_enable_buffer_1_int0_2, ir_enable_buffer_1_int1_2,
       ir_enable_buffer_1_int2_2, ir_enable_buffer_1_int3_2, ir_enable_buffer_1_int4_2,
       ir_enable_buffer_1_int5_2, ir_enable_buffer_1_int6_2, ir_enable_buffer_1_int7_2, irarb_1_ia0,
       irarb_1_ia1, irarb_1_ia2, irarb_1_ia3, irarb_1_ia4, irarb_1_ia5, irarb_1_ia6, irarb_1_ia7, IRQ,
       keypad_controller_1_p11, keypad_controller_1_p12, keypad_controller_1_p13, keypad_controller_1_p14,
       keypad_controller_1_p15, LEFT_out, mem, not_1_out, RAM_Global, RAM_Paged, rd_wr_prime, RIGHT_out, ROM,
       UP_out, Vector;
  wire [2:0] vec;
  wire [3:0] I_O_Address;
  wire [6:0] RAM_Global_Address;
  wire [7:0] Address_Bus, cdm_8_mark5_1_data_out, controlled_buffer_1_out, controlled_buffer_3_out, Data_Bus,
       PC, PS, R0, R1, R2, R3, register_1_q, ROM_Address_Hi, SP;
  wire [11:0] bit_extender_1_out;
  wire [14:0] RAM_Paged_Address;
  wire [31:0] display_controller_color_1_colomn_scan_b, display_controller_color_1_colomn_scan_g,
       display_controller_color_1_colomn_scan_r, display_controller_color_1_data_blue,
       display_controller_color_1_data_green, display_controller_color_1_data_red,
       display_controller_mono_1_colomn_scan, display_controller_mono_1_data;

  Button LEFT (.out(LEFT_out));
  // Probe on R0
  // Probe on R0
  // Probe on R0
  // Probe on R1
  // Probe on R1
  // Probe on R1
  // Probe on R2
  // Probe on R2
  // Probe on R2
  // Probe on R3
  // Probe on R3
  // Probe on R3
  Button UP (.out(UP_out));
  Button RIGHT (.out(RIGHT_out));
  Button DOWN (.out(DOWN_out));
  // Probe on PC
  // Probe on R0
  // Probe on SP
  // Probe on R1
  // Probe on R2
  // Probe on R3
  Clock clock_1 (.out(Clock));
  // Probe on PC
  // Probe on PC
  // Probe on SP
  // Probe on SP
  // Probe on PS
  // Keypad_Controller keypad_controller_1: pin names not known; wires that end beside it: Data_Bus, Clock, UP_out, rd_wr_prime, DOWN_out, I_O_Address, LEFT_out, I_O, RIGHT_out, 4'b1100, keypad_controller_1_p11, keypad_controller_1_p12, keypad_controller_1_p13, keypad_controller_1_p14, keypad_controller_1_p15
  Button button_1 (.out(keypad_controller_1_p11));
  Button button_2 (.out(keypad_controller_1_p12));
  Button button_3 (.out(keypad_controller_1_p15));
  Button button_4 (.out(keypad_controller_1_p14));
  IrArb irarb_1 (
    .IAck(IAck), .Vector(vec), .IRQ(IRQ), .INT0(ir_enable_buffer_1_int0_2), .IA0(irarb_1_ia0),
    .INT1(ir_enable_buffer_1_int1_2), .IA1(irarb_1_ia1), .INT2(ir_enable_buffer_1_int2_2), .IA2(irarb_1_ia2),
    .INT3(ir_enable_buffer_1_int3_2), .IA3(irarb_1_ia3), .INT4(ir_enable_buffer_1_int4_2), .IA4(irarb_1_ia4),
    .INT5(ir_enable_buffer_1_int5_2), .IA5(irarb_1_ia5), .INT6(ir_enable_buffer_1_int6_2), .IA6(irarb_1_ia6),
    .INT7(ir_enable_buffer_1_int7_2), .IA7(irarb_1_ia7));
  Ir_Enable_Buffer ir_enable_buffer_1 (
    .Data_Bus_In(Data_Bus), .rd_wr_prime(rd_wr_prime), .IO_Address(I_O_Address), .IO(I_O),
    .Device_Address(4'b0000), .Clock(Clock), .Data_Bus_Out(Data_Bus), .INT0(keypad_controller_1_p13),
    .INT1(button_7_out), .INT2(button_6_out), .INT3(button_5_out), .INT4(button_11_out), .INT5(button_8_out),
    .INT6(button_10_out), .INT7(button_9_out), .INT0_2(ir_enable_buffer_1_int0_2), .IA0(irarb_1_ia0),
    .INT1_2(ir_enable_buffer_1_int1_2), .IA1(irarb_1_ia1), .INT2_2(ir_enable_buffer_1_int2_2),
    .IA2(irarb_1_ia2), .INT3_2(ir_enable_buffer_1_int3_2), .IA3(irarb_1_ia3),
    .INT4_2(ir_enable_buffer_1_int4_2), .IA4(irarb_1_ia4), .INT5_2(ir_enable_buffer_1_int5_2),
    .IA5(irarb_1_ia5), .INT6_2(ir_enable_buffer_1_int6_2), .IA6(irarb_1_ia6),
    .INT7_2(ir_enable_buffer_1_int7_2), .IA7(irarb_1_ia7), .Enable(IR_Enable));  // open: IA0_2, IA1_2, IA2_2, IA3_2, IA4_2, IA5_2, IA6_2, IA7_2
  Button button_5 (.out(button_5_out));
  Button button_6 (.out(button_6_out));
  Button button_7 (.out(button_7_out));
  CdM_8_mark5 cdm_8_mark5_1 (
    .clock(Clock), .addr(Address_Bus), .mem_read(rd_wr_prime), .mem_cycle(mem),
    .data_inst(cdm_8_mark5_1_data_inst), .data_out(cdm_8_mark5_1_data_out),
    .data_in(controlled_buffer_1_out), .r0(R0), .r1(R1), .r2(R2), .r3(R3), .PC(PC), .SP(SP), .PS(PS),
    .IAck(IAck), .IRQ(IRQ), .vec(vec));
  assign controlled_buffer_1_out = rd_wr_prime ? Data_Bus : 8'bz;  // Controlled_Buffer controlled_buffer_1
  Button button_8 (.out(button_8_out));
  Button button_9 (.out(button_9_out));
  Button button_10 (.out(button_10_out));
  Button button_11 (.out(button_11_out));
  Address_Decoder address_decoder_1 (
    .data_ins_prime(cdm_8_mark5_1_data_inst), .memory(mem), .Address_Bus(Address_Bus), .Inst(Inst),
    .Data(Data), .Vector(Vector), .I_O(I_O), .ROM(ROM), .RAM_Global(RAM_Global), .RAM_Paged(RAM_Paged),
    .I_O_Address(I_O_Address));
  assign Data_Bus = not_1_out ? cdm_8_mark5_1_data_out : 8'bz;  // Controlled_Buffer controlled_buffer_2
  not not_1 (not_1_out, rd_wr_prime);
  RAM_Controller ram_controller_1 (
    .Clock(Clock), .rd_wr_prime(rd_wr_prime), .IO_Address(I_O_Address), .IO(I_O), .Device_Address(4'b1110),
    .Data_Bus_In(Data_Bus), .Data_Bus_Out(Data_Bus), .Address_Bus(Address_Bus),
    .RAM_Global_Address(RAM_Global_Address), .RAM_Paged_Address(RAM_Paged_Address));
  Bit_Extender #(.in_width(15), .out_width(12)) bit_extender_1 (.in(RAM_Paged_Address), .out(bit_extender_1_out));
  ROM_Controller rom_controller_1 (
    .Clock(Clock), .rd_wr_prime(rd_wr_prime), .IO_Address(I_O_Address), .IO(I_O), .Device_Address(4'b1000),
    .ISR_Bank(8'h5), .Data_Bus_In(Data_Bus), .Data_Bus_Out(Data_Bus), .Addrerss_Out(ROM_Address_Hi),
    .IAck(IAck), .IR_Enable(IR_Enable));
  RAM #(.addrWidth(7)) ram_1 (
    .addr(RAM_Global_Address), .data(Data_Bus), .sel(RAM_Global), .clk(Clock), .ld(rd_wr_prime));  // open: clr
  RAM #(.addrWidth(12)) ram_2 (
    .addr(bit_extender_1_out), .data(Data_Bus), .sel(RAM_Paged), .clk(Clock), .ld(rd_wr_prime));  // open: clr
  Display_Controller_Color display_controller_color_1 (
    .Data_Bus_In(Data_Bus), .Data_Bus_Out(Data_Bus), .Clock(Clock), .rd_wr_prime(rd_wr_prime),
    .IO_Address(I_O_Address), .IO(I_O), .Device_Address(4'b1010), .Fast_Clock(Clock),
    .Colomn_Scan_R(display_controller_color_1_colomn_scan_r), .Data_Red(display_controller_color_1_data_red),
    .Colomn_Scan_G(display_controller_color_1_colomn_scan_g),
    .Colomn_Scan_B(display_controller_color_1_colomn_scan_b),
    .Data_Green(display_controller_color_1_data_green), .Data_Blue(display_controller_color_1_data_blue));
  // DotMatrix #(.inputtype("select"), .matrixcols(32), .matrixrows(32), .persist(64)) dotmatrix_1: pin names not known; wires that end beside it: display_controller_color_1_colomn_scan_r, display_controller_color_1_data_red
  // DotMatrix #(.inputtype("select"), .matrixcols(32), .matrixrows(32), .persist(64)) dotmatrix_2: pin names not known; wires that end beside it: display_controller_color_1_colomn_scan_g, display_controller_color_1_data_green
  // DotMatrix #(.inputtype("select"), .matrixcols(32), .matrixrows(32), .persist(64)) dotmatrix_3: pin names not known; wires that end beside it: display_controller_color_1_colomn_scan_b, display_controller_color_1_data_blue
  Math_Coprocessor math_coprocessor_1 (
    .Data_Bus_In(Data_Bus), .Data_Bus_Out(Data_Bus), .Clock(Clock), .rd_wr_prime(rd_wr_prime),
    .IO_Address(I_O_Address), .IO(I_O), .Device_Address(4'b0101));
  Comparator #(.width(4), .mode("unsigned")) comparator_1 (
    .a(I_O_Address), .b(4'b0001), .eq(comparator_1_eq));  // open: gt, lt
  and and_1 (and_1_out, I_O, comparator_1_eq);
  // RAM ram_3: pin names not known; wires that end beside it: {ROM_Address_Hi[3:0], Address_Bus}, ROM, Data_Bus
  and and_2 (and_2_out, and_1_out, ~rd_wr_prime);  // AND_Gate
  and and_3 (and_3_out, and_1_out, rd_wr_prime);
  assign controlled_buffer_3_out = and_2_out ? Data_Bus : 8'bz;  // Controlled_Buffer controlled_buffer_3
  Register register_1 (.D(controlled_buffer_3_out), .Q(register_1_q), .clk(Clock), .clr(button_12_out));  // open: en
  Button button_12 (.out(button_12_out));
  assign Data_Bus = and_3_out ? register_1_q : 8'bz;  // Controlled_Buffer controlled_buffer_4
  Display_Controller_Mono display_controller_mono_1 (
    .Data_Bus_In(Data_Bus), .Clock(Clock), .rd_wr_prime(rd_wr_prime), .IO_Address(I_O_Address), .IO(I_O),
    .Device_Address(4'b1010), .Fast_Clock(Clock), .Colomn_Scan(display_controller_mono_1_colomn_scan),
    .Data(display_controller_mono_1_data));  // open: Data_Bus_Out
  Hex_Digit_Display hex_digit_display_1 (.value(register_1_q[3:0]));  // open: dp
  Hex_Digit_Display hex_digit_display_2 (.value(register_1_q[7:4]));  // open: dp
  // DotMatrix #(.inputtype("select"), .matrixcols(32), .matrixrows(32), .persist(64)) dotmatrix_4: pin names not known; wires that end beside it: display_controller_mono_1_colomn_scan, display_controller_mono_1_data
endmodule

module Address_Decoder (
  input  data_ins_prime,
  input  memory,
  input  [7:0] Address_Bus,
  output Inst,
  output Data,
  output Vector,
  output I_O,
  output ROM,
  output RAM_Global,
  output RAM_Paged,
  output [3:0] I_O_Address
);

  wire [1:1] and_1_out;

  and and_1 (and_1_out[1], Address_Bus[4], Address_Bus[5], Address_Bus[6], Address_Bus[7]);
  Decoder #(.select(2), .disabled(0)) decoder_1 (
    .out0(Inst), .out1(Data), .out2(Vector), .out3(I_O), .sel({and_1_out[1], data_ins_prime}), .en(memory));
  Demultiplexer #(.disabled(0), .enable("false")) demultiplexer_1 (
    .out0(RAM_Global), .out1(RAM_Paged), .in(Data), .sel(Address_Bus[7]));
  or or_1 (ROM, Inst, Vector);

  assign I_O_Address = Address_Bus[3:0];

  // Other names for the same wires on the sheet: Hi_Bit = Address_Bus[7]; mem = memory; RAM_Low = RAM_Global
endmodule

module IrC_2reg (
  input  rd_wr_prime,
  input  [3:0] R1_Address,
  input  [7:0] Data_Bus_In,
  input  [3:0] R2_Address,
  input  [3:0] I_O_Address,
  input  I_O,
  input  Clock,
  input  [3:0] Vect_Address,
  input  Vector,
  output [7:0] Data_Bus_Out
);

  wire and_2_out, and_3_out, and_4_out, and_5_out, and_6_out, and_7_out, and_8_out, and_9_out, and_10_out,
       and_11_out, and_12_out, and_13_out, comparator_1_eq, comparator_2_eq, decoder_1_out0, decoder_1_out1,
       decoder_1_out2, decoder_1_out3, decoder_1_out4, decoder_1_out5, decoder_1_out6, decoder_1_out7,
       decoder_2_out0, decoder_2_out1, decoder_2_out2, decoder_2_out3, decoder_2_out4, decoder_2_out5,
       decoder_2_out6, decoder_2_out7, not_1_out, read;
  wire [7:0] controlled_buffer_1_out, controlled_buffer_3_out, controlled_buffer_5_out,
       controlled_buffer_6_out, multiplexer_1_out, register_1_q, register_2_q, register_3_q, register_4_q,
       register_5_q, register_6_q, register_7_q, register_8_q, register_9_q;

  assign controlled_buffer_1_out = not_1_out ? Data_Bus_In : 8'bz;  // Controlled_Buffer controlled_buffer_1
  not not_1 (not_1_out, rd_wr_prime);
  assign Data_Bus_Out = rd_wr_prime ? multiplexer_1_out : 8'bz;  // Controlled_Buffer controlled_buffer_2
  and and_1 (read, Vector, rd_wr_prime);
  Comparator #(.width(4), .mode("unsigned")) comparator_1 (
    .a(R1_Address), .b(I_O_Address), .eq(comparator_1_eq));  // open: gt, lt
  and and_2 (and_2_out, comparator_1_eq, I_O);
  Decoder #(.select(3), .enable("false")) decoder_1 (
    .out0(decoder_1_out0), .out1(decoder_1_out1), .out2(decoder_1_out2), .out3(decoder_1_out3),
    .out4(decoder_1_out4), .out5(decoder_1_out5), .out6(decoder_1_out6), .out7(decoder_1_out7),
    .sel(Vect_Address[3:1]));
  and and_3 (and_3_out, and_2_out, ~rd_wr_prime);  // AND_Gate
  assign controlled_buffer_3_out = and_3_out ? controlled_buffer_1_out : 8'bz;  // Controlled_Buffer controlled_buffer_3
  Register register_1 (.D(controlled_buffer_3_out), .Q(register_1_q), .clk(Clock));  // open: en, clr
  and and_4 (and_4_out, and_2_out, rd_wr_prime);
  assign controlled_buffer_1_out = and_4_out ? register_1_q : 8'bz;  // Controlled_Buffer controlled_buffer_4
  Comparator #(.width(4), .mode("unsigned")) comparator_2 (
    .a(R2_Address), .b(I_O_Address), .eq(comparator_2_eq));  // open: gt, lt
  Multiplexer #(.width(8), .disabled(0), .enable("false")) multiplexer_1 (
    .in0(controlled_buffer_6_out), .in1(controlled_buffer_5_out), .out(multiplexer_1_out),
    .sel(Vect_Address[0]));
  Decoder #(.select(3), .enable("false")) decoder_2 (
    .out0(decoder_2_out0), .out1(decoder_2_out1), .out2(decoder_2_out2), .out3(decoder_2_out3),
    .out4(decoder_2_out4), .out5(decoder_2_out5), .out6(decoder_2_out6), .out7(decoder_2_out7),
    .sel(register_1_q[2:0]));
  and and_5 (and_5_out, comparator_2_eq, I_O, Clock);
  assign controlled_buffer_5_out = read ? {8{1'b0}} : 8'bz;  // Controlled_Buffer controlled_buffer_5
  Register register_2 (
    .D(controlled_buffer_1_out), .en(decoder_2_out0), .Q(register_2_q), .clk(and_5_out));  // open: clr
  and and_6 (and_6_out, read, decoder_1_out0);
  assign controlled_buffer_6_out = and_6_out ? register_2_q : 8'bz;  // Controlled_Buffer controlled_buffer_6
  Register register_3 (
    .D(controlled_buffer_1_out), .en(decoder_2_out1), .Q(register_3_q), .clk(and_5_out));  // open: clr
  and and_7 (and_7_out, read, decoder_1_out1);
  assign controlled_buffer_6_out = and_7_out ? register_3_q : 8'bz;  // Controlled_Buffer controlled_buffer_7
  Register register_4 (
    .D(controlled_buffer_1_out), .en(decoder_2_out2), .Q(register_4_q), .clk(and_5_out));  // open: clr
  and and_8 (and_8_out, read, decoder_1_out2);
  assign controlled_buffer_6_out = and_8_out ? register_4_q : 8'bz;  // Controlled_Buffer controlled_buffer_8
  Register register_5 (
    .D(controlled_buffer_1_out), .en(decoder_2_out3), .Q(register_5_q), .clk(and_5_out));  // open: clr
  and and_9 (and_9_out, read, decoder_1_out3);
  assign controlled_buffer_6_out = and_9_out ? register_5_q : 8'bz;  // Controlled_Buffer controlled_buffer_9
  Register register_6 (
    .D(controlled_buffer_1_out), .en(decoder_2_out4), .Q(register_6_q), .clk(and_5_out));  // open: clr
  and and_10 (and_10_out, read, decoder_1_out4);
  assign controlled_buffer_6_out = and_10_out ? register_6_q : 8'bz;  // Controlled_Buffer controlled_buffer_10
  Register register_7 (
    .D(controlled_buffer_1_out), .en(decoder_2_out5), .Q(register_7_q), .clk(and_5_out));  // open: clr
  and and_11 (and_11_out, read, decoder_1_out5);
  assign controlled_buffer_6_out = and_11_out ? register_7_q : 8'bz;  // Controlled_Buffer controlled_buffer_11
  Register register_8 (
    .D(controlled_buffer_1_out), .en(decoder_2_out6), .Q(register_8_q), .clk(and_5_out));  // open: clr
  and and_12 (and_12_out, read, decoder_1_out6);
  assign controlled_buffer_6_out = and_12_out ? register_8_q : 8'bz;  // Controlled_Buffer controlled_buffer_12
  Register register_9 (
    .D(controlled_buffer_1_out), .en(decoder_2_out7), .Q(register_9_q), .clk(and_5_out));  // open: clr
  and and_13 (and_13_out, read, decoder_1_out7);
  assign controlled_buffer_6_out = and_13_out ? register_9_q : 8'bz;  // Controlled_Buffer controlled_buffer_13

  // Other names for the same wires on the sheet: Cl = Clock; rw_prime = rd_wr_prime; mux = Vect_Address[0]
endmodule

module IrC_1reg (
  input  rd_wr_prime,
  input  [3:0] Device_Address,
  input  [7:0] Data_Bus_In,
  input  [3:0] I_O_Address,
  input  I_O,
  input  Clock,
  input  [3:0] Vect_Address,
  input  Vector,
  output [7:0] Data_Bus_Out
);

  wire and_2_out, and_3_out, and_4_out, and_5_out, and_6_out, and_8_out, and_9_out, and_10_out, and_11_out,
       and_12_out, and_13_out, and_14_out, and_15_out, and_16_out, comparator_1_eq, d_ff_1_q, d_ff_1_qn,
       decoder_1_out0, decoder_1_out1, decoder_2_out0, decoder_2_out1, decoder_2_out2, decoder_2_out3,
       decoder_2_out4, decoder_2_out5, decoder_2_out6, decoder_2_out7, decoder_3_out0, decoder_3_out1,
       decoder_3_out2, decoder_3_out3, decoder_3_out4, decoder_3_out5, decoder_3_out6, decoder_3_out7, Latch,
       not_1_out, read;
  wire [7:0] controlled_buffer_1_out, controlled_buffer_3_out, controlled_buffer_5_out,
       controlled_buffer_6_out, multiplexer_1_out, register_1_q, register_2_q, register_3_q, register_4_q,
       register_5_q, register_6_q, register_7_q, register_8_q, register_9_q;

  D_Flip_Flop #(.trigger("falling")) d_ff_1 (
    .clk(Latch), .D(d_ff_1_qn), .Q(d_ff_1_q), .Qn(d_ff_1_qn));  // open: preset, en, reset
  assign controlled_buffer_1_out = not_1_out ? Data_Bus_In : 8'bz;  // Controlled_Buffer controlled_buffer_1
  not not_1 (not_1_out, rd_wr_prime);
  assign Data_Bus_Out = rd_wr_prime ? multiplexer_1_out : 8'bz;  // Controlled_Buffer controlled_buffer_2
  and and_1 (read, Vector, rd_wr_prime);
  Decoder #(.enable("false")) decoder_1 (.out0(decoder_1_out0), .out1(decoder_1_out1), .sel(d_ff_1_q));
  and and_2 (and_2_out, decoder_1_out0, and_3_out);
  Comparator #(.width(4), .mode("unsigned")) comparator_1 (
    .a(Device_Address), .b(I_O_Address), .eq(comparator_1_eq));  // open: gt, lt
  and and_3 (and_3_out, comparator_1_eq, I_O);
  Decoder #(.select(3), .enable("false")) decoder_2 (
    .out0(decoder_2_out0), .out1(decoder_2_out1), .out2(decoder_2_out2), .out3(decoder_2_out3),
    .out4(decoder_2_out4), .out5(decoder_2_out5), .out6(decoder_2_out6), .out7(decoder_2_out7),
    .sel(Vect_Address[3:1]));
  and and_4 (and_4_out, and_2_out, ~rd_wr_prime);  // AND_Gate
  assign controlled_buffer_3_out = and_4_out ? controlled_buffer_1_out : 8'bz;  // Controlled_Buffer controlled_buffer_3
  and and_5 (and_5_out, and_2_out, rd_wr_prime);
  Register register_1 (.D(controlled_buffer_3_out), .Q(register_1_q), .clk(Clock));  // open: en, clr
  assign controlled_buffer_1_out = and_5_out ? register_1_q : 8'bz;  // Controlled_Buffer controlled_buffer_4
  and and_6 (and_6_out, decoder_1_out1, and_3_out);
  and and_7 (Latch, Clock, and_3_out);
  Multiplexer #(.width(8), .disabled(0), .enable("false")) multiplexer_1 (
    .in0(controlled_buffer_6_out), .in1(controlled_buffer_5_out), .out(multiplexer_1_out),
    .sel(Vect_Address[0]));
  Decoder #(.select(3), .enable("false")) decoder_3 (
    .out0(decoder_3_out0), .out1(decoder_3_out1), .out2(decoder_3_out2), .out3(decoder_3_out3),
    .out4(decoder_3_out4), .out5(decoder_3_out5), .out6(decoder_3_out6), .out7(decoder_3_out7),
    .sel(register_1_q[2:0]));
  and and_8 (and_8_out, and_6_out, I_O, Clock);
  assign controlled_buffer_5_out = read ? {8{1'b0}} : 8'bz;  // Controlled_Buffer controlled_buffer_5
  Register register_2 (
    .D(controlled_buffer_1_out), .en(decoder_3_out0), .Q(register_2_q), .clk(and_8_out));  // open: clr
  and and_9 (and_9_out, read, decoder_2_out0);
  assign controlled_buffer_6_out = and_9_out ? register_2_q : 8'bz;  // Controlled_Buffer controlled_buffer_6
  Register register_3 (
    .D(controlled_buffer_1_out), .en(decoder_3_out1), .Q(register_3_q), .clk(and_8_out));  // open: clr
  and and_10 (and_10_out, read, decoder_2_out1);
  assign controlled_buffer_6_out = and_10_out ? register_3_q : 8'bz;  // Controlled_Buffer controlled_buffer_7
  Register register_4 (
    .D(controlled_buffer_1_out), .en(decoder_3_out2), .Q(register_4_q), .clk(and_8_out));  // open: clr
  and and_11 (and_11_out, read, decoder_2_out2);
  assign controlled_buffer_6_out = and_11_out ? register_4_q : 8'bz;  // Controlled_Buffer controlled_buffer_8
  Register register_5 (
    .D(controlled_buffer_1_out), .en(decoder_3_out3), .Q(register_5_q), .clk(and_8_out));  // open: clr
  and and_12 (and_12_out, read, decoder_2_out3);
  assign controlled_buffer_6_out = and_12_out ? register_5_q : 8'bz;  // Controlled_Buffer controlled_buffer_9
  Register register_6 (
    .D(controlled_buffer_1_out), .en(decoder_3_out4), .Q(register_6_q), .clk(and_8_out));  // open: clr
  and and_13 (and_13_out, read, decoder_2_out4);
  assign controlled_buffer_6_out = and_13_out ? register_6_q : 8'bz;  // Controlled_Buffer controlled_buffer_10
  Register register_7 (
    .D(controlled_buffer_1_out), .en(decoder_3_out5), .Q(register_7_q), .clk(and_8_out));  // open: clr
  and and_14 (and_14_out, read, decoder_2_out5);
  assign controlled_buffer_6_out = and_14_out ? register_7_q : 8'bz;  // Controlled_Buffer controlled_buffer_11
  Register register_8 (
    .D(controlled_buffer_1_out), .en(decoder_3_out6), .Q(register_8_q), .clk(and_8_out));  // open: clr
  and and_15 (and_15_out, read, decoder_2_out6);
  assign controlled_buffer_6_out = and_15_out ? register_8_q : 8'bz;  // Controlled_Buffer controlled_buffer_12
  Register register_9 (
    .D(controlled_buffer_1_out), .en(decoder_3_out7), .Q(register_9_q), .clk(and_8_out));  // open: clr
  and and_16 (and_16_out, read, decoder_2_out7);
  assign controlled_buffer_6_out = and_16_out ? register_9_q : 8'bz;  // Controlled_Buffer controlled_buffer_13

  // Other names for the same wires on the sheet: Cl = Clock; rw_prime = rd_wr_prime; mux = Vect_Address[0]
endmodule

module Ir_Enable_Buffer (
  input  [7:0] Data_Bus_In,
  input  rd_wr_prime,
  input  [3:0] IO_Address,
  input  IO,
  input  [3:0] Device_Address,
  input  Clock,
  input  Enable,
  input  IA0,
  input  IA1,
  input  IA2,
  input  IA3,
  input  IA4,
  input  IA5,
  input  IA6,
  input  IA7,
  input  INT0,
  input  INT1,
  input  INT2,
  input  INT3,
  input  INT4,
  input  INT5,
  input  INT6,
  input  INT7,
  output [7:0] Data_Bus_Out,
  output INT0_2,
  output INT1_2,
  output INT2_2,
  output INT3_2,
  output INT4_2,
  output INT5_2,
  output INT6_2,
  output INT7_2,
  output IA0_2,
  output IA1_2,
  output IA2_2,
  output IA3_2,
  output IA4_2,
  output IA5_2,
  output IA6_2,
  output IA7_2
);

  wire and_1_out, and_2_out, and_4_out, comparator_1_eq;
  wire [7:0] and_3_out, bit_extender_1_out, controlled_buffer_1_out, register_1_q;

  Comparator #(.width(4), .mode("unsigned")) comparator_1 (
    .a(IO_Address), .b(Device_Address), .eq(comparator_1_eq));  // open: gt, lt
  and and_1 (and_1_out, IO, comparator_1_eq);
  assign bit_extender_1_out = {{7{Enable}}, Enable};  // Bit_Extender bit_extender_1
  and and_2 (and_2_out, and_1_out, ~rd_wr_prime);  // AND_Gate
  Register register_1 (.D(controlled_buffer_1_out), .Q(register_1_q), .clk(Clock));  // open: en, clr
  assign controlled_buffer_1_out = and_2_out ? Data_Bus_In : 8'bz;  // Controlled_Buffer controlled_buffer_1
  assign and_3_out = bit_extender_1_out & register_1_q;  // AND_Gate and_3, 8 bits wide
  and and_4 (and_4_out, and_1_out, rd_wr_prime);
  assign Data_Bus_Out = and_4_out ? register_1_q : 8'bz;  // Controlled_Buffer controlled_buffer_2
  and and_5 (INT0_2, and_3_out[0], INT0);
  and and_6 (INT1_2, and_3_out[1], INT1);
  and and_7 (INT2_2, and_3_out[2], INT2);
  and and_8 (INT3_2, and_3_out[3], INT3);
  and and_9 (INT4_2, and_3_out[4], INT4);
  and and_10 (INT5_2, and_3_out[5], INT5);
  and and_11 (INT6_2, and_3_out[6], INT6);
  and and_12 (INT7_2, and_3_out[7], INT7);

  assign IA0_2 = IA0;
  assign IA1_2 = IA1;
  assign IA2_2 = IA2;
  assign IA3_2 = IA3;
  assign IA4_2 = IA4;
  assign IA5_2 = IA5;
  assign IA6_2 = IA6;
  assign IA7_2 = IA7;

  // Notes on the sheet:
  //   INT6_2: pull=down
  //   INT7_2: pull=down
  //   IA3: pull=down
  //   IA2: pull=down
  //   INT5: pull=down
  //   INT7: pull=down
  //   INT6: pull=down
  //   INT2_2: pull=down
  //   IA7: pull=down
  //   INT4_2: pull=down
  //   IA1: pull=down
  //   IA6: pull=down
  //   INT5_2: pull=down
  //   INT0: pull=down
  //   Enable: pull=up
  //   INT0_2: pull=down
  //   IA5: pull=down
  //   IA4: pull=down
  //   INT1_2: pull=down
  //   INT2: pull=down
  //   INT3_2: pull=down
  //   INT1: pull=down
  //   INT4: pull=down
  //   INT3: pull=down
  //   IA0: pull=down
endmodule

module IrArb (
  input  IAck,
  input  INT0,
  input  INT1,
  input  INT2,
  input  INT3,
  input  INT4,
  input  INT5,
  input  INT6,
  input  INT7,
  output [2:0] Vector,
  output IRQ,
  output IA0,
  output IA1,
  output IA2,
  output IA3,
  output IA4,
  output IA5,
  output IA6,
  output IA7
);

  wire and_1_out, and_2_out, and_3_out, and_4_out, and_5_out, and_6_out, front_detector_long_1_out,
       front_detector_long_2_out, front_detector_long_3_out, front_detector_long_4_out,
       front_detector_long_5_out, front_detector_long_6_out, front_detector_long_7_out,
       front_detector_long_8_out, front_detector_long_9_out, front_detector_long_10_out,
       front_detector_long_11_out, front_detector_long_12_out, n8_or_1_out, n8_or_2_out, not_1_out, or_1_out,
       priority_encoder_1_p2, priority_encoder_1_p3, priority_encoder_1_p4, priority_encoder_1_p5,
       priority_encoder_1_p6, priority_encoder_1_p7, priority_encoder_1_p8, priority_encoder_1_p9,
       s_r_ff_1_qn, s_r_ff_2_qn, s_r_ff_3_qn, s_r_ff_4_qn, s_r_ff_5_qn, s_r_ff_6_qn, s_r_ff_7_qn, s_r_ff_8_qn;
  wire [2:0] not_2_out, pull_resistor_1_node;

  not not_1 (not_1_out, IAck);
  Front_Detector_Long front_detector_long_1 (.In(not_1_out), .Out(front_detector_long_1_out));
  Front_Detector_Long front_detector_long_2 (.In(front_detector_long_3_out), .Out(front_detector_long_2_out));
  Front_Detector_Long front_detector_long_3 (.In(or_1_out), .Out(front_detector_long_3_out));
  or or_1 (or_1_out, n8_or_1_out, front_detector_long_1_out);
  assign not_2_out = ~pull_resistor_1_node;  // NOT_Gate not_2, 3 bits wide
  Pull_Resistor pull_resistor_1 (.node(pull_resistor_1_node));
  Front_Detector_Long front_detector_long_4 (.In(front_detector_long_1_out), .Out(front_detector_long_4_out));
  // Priority_Encoder #(.disabled(0)) priority_encoder_1: pin names not known; wires that end beside it: pull_resistor_1_node, priority_encoder_1_p2, priority_encoder_1_p3, priority_encoder_1_p4, priority_encoder_1_p5, priority_encoder_1_p6, priority_encoder_1_p7, priority_encoder_1_p8, priority_encoder_1_p9
  _8_OR u_8_or_1 (
    .Out(n8_or_1_out), .In1(front_detector_long_5_out), .In2(front_detector_long_6_out),
    .In3(front_detector_long_7_out), .In4(front_detector_long_8_out), .In5(front_detector_long_9_out),
    .In6(front_detector_long_10_out), .In7(front_detector_long_11_out), .In8(front_detector_long_12_out));
  Register #(.width(3), .trigger("falling")) register_1 (
    .D(not_2_out), .Q(Vector), .clk(front_detector_long_2_out));  // open: en, clr
  _8_OR u_8_or_2 (
    .Out(n8_or_2_out), .In1(priority_encoder_1_p9), .In2(priority_encoder_1_p8), .In3(priority_encoder_1_p7),
    .In4(priority_encoder_1_p6), .In5(priority_encoder_1_p5), .In6(priority_encoder_1_p4),
    .In7(priority_encoder_1_p3), .In8(priority_encoder_1_p2));
  Front_Detector_Long front_detector_long_5 (.In(INT0), .Out(front_detector_long_5_out));
  D_Flip_Flop #(.trigger("falling")) d_ff_1 (
    .clk(front_detector_long_2_out), .D(n8_or_2_out), .Q(IRQ), .reset(front_detector_long_4_out));  // open: Qn, preset, en
  S_R_Flip_Flop s_r_ff_1 (
    .S(1'b0), .clk(front_detector_long_1_out), .R(front_detector_long_1_out), .Q(priority_encoder_1_p9),
    .Qn(s_r_ff_1_qn), .preset(front_detector_long_5_out), .en(1'b1));  // open: reset
  Front_Detector_Short front_detector_short_1 (.In(s_r_ff_1_qn), .Out(IA0));
  Front_Detector_Long front_detector_long_6 (.In(INT1), .Out(front_detector_long_6_out));
  S_R_Flip_Flop s_r_ff_2 (
    .S(1'b0), .clk(front_detector_long_1_out), .R(front_detector_long_1_out), .Q(priority_encoder_1_p8),
    .Qn(s_r_ff_2_qn), .preset(front_detector_long_6_out), .en(s_r_ff_1_qn));  // open: reset
  and and_1 (and_1_out, s_r_ff_2_qn, s_r_ff_1_qn);
  Front_Detector_Short front_detector_short_2 (.In(s_r_ff_2_qn), .Out(IA1));
  Front_Detector_Long front_detector_long_7 (.In(INT2), .Out(front_detector_long_7_out));
  S_R_Flip_Flop s_r_ff_3 (
    .S(1'b0), .clk(front_detector_long_1_out), .R(front_detector_long_1_out), .Q(priority_encoder_1_p7),
    .Qn(s_r_ff_3_qn), .preset(front_detector_long_7_out), .en(and_1_out));  // open: reset
  and and_2 (and_2_out, s_r_ff_3_qn, and_1_out);
  Front_Detector_Short front_detector_short_3 (.In(s_r_ff_3_qn), .Out(IA2));
  S_R_Flip_Flop s_r_ff_4 (
    .S(1'b0), .clk(front_detector_long_1_out), .R(front_detector_long_1_out), .Q(priority_encoder_1_p6),
    .Qn(s_r_ff_4_qn), .preset(front_detector_long_8_out), .en(and_2_out));  // open: reset
  Front_Detector_Short front_detector_short_4 (.In(s_r_ff_4_qn), .Out(IA3));
  Front_Detector_Long front_detector_long_8 (.In(INT3), .Out(front_detector_long_8_out));
  S_R_Flip_Flop s_r_ff_5 (
    .S(1'b0), .clk(front_detector_long_1_out), .R(front_detector_long_1_out), .Q(priority_encoder_1_p5),
    .Qn(s_r_ff_5_qn), .preset(front_detector_long_9_out), .en(and_3_out));  // open: reset
  and and_3 (and_3_out, s_r_ff_4_qn, and_2_out);
  Front_Detector_Short front_detector_short_5 (.In(s_r_ff_5_qn), .Out(IA4));
  Front_Detector_Long front_detector_long_9 (.In(INT4), .Out(front_detector_long_9_out));
  S_R_Flip_Flop s_r_ff_6 (
    .S(1'b0), .clk(front_detector_long_1_out), .R(front_detector_long_1_out), .Q(priority_encoder_1_p4),
    .Qn(s_r_ff_6_qn), .preset(front_detector_long_10_out), .en(and_4_out));  // open: reset
  and and_4 (and_4_out, s_r_ff_5_qn, and_3_out);
  Front_Detector_Short front_detector_short_6 (.In(s_r_ff_6_qn), .Out(IA5));
  Front_Detector_Long front_detector_long_10 (.In(INT5), .Out(front_detector_long_10_out));
  S_R_Flip_Flop s_r_ff_7 (
    .S(1'b0), .clk(front_detector_long_1_out), .R(front_detector_long_1_out), .Q(priority_encoder_1_p3),
    .Qn(s_r_ff_7_qn), .preset(front_detector_long_11_out), .en(and_5_out));  // open: reset
  and and_5 (and_5_out, s_r_ff_6_qn, and_4_out);
  Front_Detector_Short front_detector_short_7 (.In(s_r_ff_7_qn), .Out(IA6));
  Front_Detector_Long front_detector_long_11 (.In(INT6), .Out(front_detector_long_11_out));
  S_R_Flip_Flop s_r_ff_8 (
    .S(1'b0), .clk(front_detector_long_1_out), .R(front_detector_long_1_out), .Q(priority_encoder_1_p2),
    .Qn(s_r_ff_8_qn), .preset(front_detector_long_12_out), .en(and_6_out));  // open: reset
  and and_6 (and_6_out, s_r_ff_7_qn, and_5_out);
  Front_Detector_Long front_detector_long_12 (.In(INT7), .Out(front_detector_long_12_out));
  Front_Detector_Short front_detector_short_8 (.In(s_r_ff_8_qn), .Out(IA7));

  // Notes on the sheet:
  //   INT5: pull=down
  //   INT4: pull=down
  //   INT2: pull=down
  //   INT3: pull=down
  //   INT0: pull=down
  //   INT1: pull=down
  //   INT7: pull=down
  //   INT6: pull=down
  //   INT7 - Lowest Priority
  //   INT0 - Highest Priority
endmodule

module IO_Reg (
  input  [7:0] Data_Bus_In,
  input  rd_wr_prime,
  input  [3:0] IO_Address,
  input  IO,
  input  [3:0] Device_Address,
  input  Clock,
  output [7:0] Data_Bus_Out,
  output [7:0] Data_Out
);

  wire and_1_out, and_2_out, and_3_out, comparator_1_eq;
  wire [7:0] controlled_buffer_1_out;

  Comparator #(.width(4), .mode("unsigned")) comparator_1 (
    .a(IO_Address), .b(Device_Address), .eq(comparator_1_eq));  // open: gt, lt
  and and_1 (and_1_out, IO, comparator_1_eq);
  and and_2 (and_2_out, and_1_out, ~rd_wr_prime);  // AND_Gate
  assign controlled_buffer_1_out = and_2_out ? Data_Bus_In : 8'bz;  // Controlled_Buffer controlled_buffer_1
  Register register_1 (.D(controlled_buffer_1_out), .Q(Data_Out), .clk(Clock));  // open: en, clr
  and and_3 (and_3_out, and_1_out, rd_wr_prime);
  assign Data_Bus_Out = and_3_out ? Data_Out : 8'bz;  // Controlled_Buffer controlled_buffer_2
endmodule

module IO_Stack (
  input  Clock,
  input  rd_wr_prime,
  input  [3:0] IO_Address,
  input  IO,
  input  [3:0] Device_Address,
  input  [7:0] Data_Bus_In,
  output [7:0] Data_Bus_Out
);

  wire and_2_out, and_3_out, comparator_1_eq, not_1_out, Select;
  wire [7:0] controlled_buffer_2_out, register_stack_1_cascade_out, register_stack_1_data_out,
       register_stack_2_cascade_out, register_stack_2_data_out, register_stack_3_cascade_out,
       register_stack_3_data_out, register_stack_4_cascade_out, register_stack_4_data_out,
       register_stack_5_data_out;

  Comparator #(.width(4), .mode("unsigned")) comparator_1 (
    .a(IO_Address), .b(Device_Address), .eq(comparator_1_eq));  // open: gt, lt
  assign Data_Bus_Out = and_3_out ? register_stack_1_data_out : 8'bz;  // Controlled_Buffer controlled_buffer_1
  and and_1 (Select, IO, comparator_1_eq);
  and and_2 (and_2_out, Select, not_1_out);
  not not_1 (not_1_out, rd_wr_prime);
  assign controlled_buffer_2_out = and_2_out ? Data_Bus_In : 8'bz;  // Controlled_Buffer controlled_buffer_2
  and and_3 (and_3_out, rd_wr_prime, Select);
  Register_Stack register_stack_1 (
    .Data_Out(register_stack_1_data_out), .Data_In(controlled_buffer_2_out), .Clock(Clock), .Enable(Select),
    .rd_wr_prime(rd_wr_prime), .Cascade_In(register_stack_2_data_out),
    .Cascade_Out(register_stack_1_cascade_out));  // open: out_8, out_9, out_10, out_11
  Register_Stack register_stack_2 (
    .Data_Out(register_stack_2_data_out), .Data_In(register_stack_1_cascade_out), .Clock(Clock),
    .Enable(Select), .rd_wr_prime(rd_wr_prime), .Cascade_In(register_stack_3_data_out),
    .Cascade_Out(register_stack_2_cascade_out));  // open: out_8, out_9, out_10, out_11
  Register_Stack register_stack_3 (
    .Data_Out(register_stack_3_data_out), .Data_In(register_stack_2_cascade_out), .Clock(Clock),
    .Enable(Select), .rd_wr_prime(rd_wr_prime), .Cascade_In(register_stack_4_data_out),
    .Cascade_Out(register_stack_3_cascade_out));  // open: out_8, out_9, out_10, out_11
  Register_Stack register_stack_4 (
    .Data_Out(register_stack_4_data_out), .Data_In(register_stack_3_cascade_out), .Clock(Clock),
    .Enable(Select), .rd_wr_prime(rd_wr_prime), .Cascade_In(register_stack_5_data_out),
    .Cascade_Out(register_stack_4_cascade_out));  // open: out_8, out_9, out_10, out_11
  Register_Stack register_stack_5 (
    .Data_Out(register_stack_5_data_out), .Data_In(register_stack_4_cascade_out), .Clock(Clock),
    .Enable(Select), .rd_wr_prime(rd_wr_prime), .Cascade_In({8{1'b0}}));  // open: out_8, out_9, out_10, out_11, Cascade_Out
endmodule

module IO_Random_Number_Generator (
  input  Clock,
  input  rd_wr_prime,
  input  [3:0] IO_Address,
  input  IO,
  input  [3:0] Device_Address,
  output [7:0] Data_Bus_Out
);

  wire and_1_out, comparator_1_eq, Select;
  wire [7:0] Data_Bus;

  Comparator #(.width(4), .mode("unsigned")) comparator_1 (
    .a(IO_Address), .b(Device_Address), .eq(comparator_1_eq));  // open: gt, lt
  assign Data_Bus_Out = and_1_out ? Data_Bus : 8'bz;  // Controlled_Buffer controlled_buffer_1
  and and_1 (and_1_out, rd_wr_prime, Select);
  and and_2 (Select, IO, comparator_1_eq);
  Random #(.trigger("falling")) random_1 (.clk(and_1_out), .out(Data_Bus));  // open: next, clr
endmodule

module Register_Stack (
  input  [7:0] Cascade_In,
  input  [7:0] Data_In,
  input  Clock,
  input  Enable,
  input  rd_wr_prime,
  output [7:0] Data_Out,
  output [7:0] Cascade_Out,
  output [7:0] out_8,
  output [7:0] out_9,
  output [7:0] out_10,
  output [7:0] out_11
);

  wire not_1_out;
  wire [7:0] controlled_buffer_1_out, controlled_buffer_3_out, controlled_buffer_5_out,
       controlled_buffer_7_out;

  not not_1 (not_1_out, rd_wr_prime);
  Register #(.trigger("falling")) register_1 (
    .D(controlled_buffer_1_out), .en(Enable), .Q(Data_Out), .clk(Clock));  // open: clr
  assign controlled_buffer_1_out = not_1_out ? Data_In : 8'bz;  // Controlled_Buffer controlled_buffer_1
  assign controlled_buffer_1_out = rd_wr_prime ? out_9 : 8'bz;  // Controlled_Buffer controlled_buffer_2
  assign controlled_buffer_3_out = not_1_out ? Data_Out : 8'bz;  // Controlled_Buffer controlled_buffer_3
  assign controlled_buffer_3_out = rd_wr_prime ? out_10 : 8'bz;  // Controlled_Buffer controlled_buffer_4
  Register #(.trigger("falling")) register_2 (
    .D(controlled_buffer_3_out), .en(Enable), .Q(out_9), .clk(Clock));  // open: clr
  assign controlled_buffer_5_out = not_1_out ? out_9 : 8'bz;  // Controlled_Buffer controlled_buffer_5
  assign controlled_buffer_5_out = rd_wr_prime ? Cascade_Out : 8'bz;  // Controlled_Buffer controlled_buffer_6
  Register #(.trigger("falling")) register_3 (
    .D(controlled_buffer_5_out), .en(Enable), .Q(out_10), .clk(Clock));  // open: clr
  assign controlled_buffer_7_out = not_1_out ? out_10 : 8'bz;  // Controlled_Buffer controlled_buffer_7
  Register #(.trigger("falling")) register_4 (
    .D(controlled_buffer_7_out), .en(Enable), .Q(Cascade_Out), .clk(Clock));  // open: clr
  assign controlled_buffer_7_out = rd_wr_prime ? Cascade_In : 8'bz;  // Controlled_Buffer controlled_buffer_8

  assign out_8 = Data_Out;
  assign out_11 = Cascade_Out;
endmodule

module _8_OR (
  input  In1,
  input  In2,
  input  In3,
  input  In4,
  input  In5,
  input  In6,
  input  In7,
  input  In8,
  output Out
);

  wire or_1_out, or_2_out, or_4_out, or_5_out, or_6_out, or_7_out;

  or or_1 (or_1_out, or_2_out, or_5_out);
  or or_2 (or_2_out, In1, In2);
  or or_3 (Out, or_1_out, or_4_out);
  or or_4 (or_4_out, or_6_out, or_7_out);
  or or_5 (or_5_out, In3, In4);
  or or_6 (or_6_out, In5, In6);
  or or_7 (or_7_out, In7, In8);
endmodule

module Front_Detector_Short (
  input  In,
  output Out
);

  wire not_1_out;

  not not_1 (not_1_out, In);
  and and_1 (Out, In, not_1_out);
endmodule

module Front_Detector_Long (
  input  In,
  output Out
);

  wire not_1_out, not_2_out, not_3_out, not_4_out, not_5_out;

  not not_1 (not_1_out, In);
  not not_2 (not_2_out, not_1_out);
  not not_3 (not_3_out, not_5_out);
  not not_4 (not_4_out, not_2_out);
  not not_5 (not_5_out, not_4_out);
  and and_1 (Out, In, not_3_out);
endmodule

module Math_Coprocessor (
  input  [7:0] Data_Bus_In,
  input  Clock,
  input  rd_wr_prime,
  input  [3:0] IO_Address,
  input  IO,
  input  [3:0] Device_Address,
  output [7:0] Data_Bus_Out
);

  wire and_1_out, and_3_out, and_4_out, and_5_out, and_6_out, bits, comparator_1_eq, comparator_2_eq,
       comparator_2_gt, comparator_2_lt, comparator_3_eq, comparator_3_gt, comparator_3_lt, decoder_1_out2,
       decoder_2_out3, decoder_2_out5, not_1_out, not_2_out, or_1_out, Select;
  wire [1:0] counter_1_q, priority_encoder_1_out, priority_encoder_2_out;
  wire [2:0] counter_2_q, op;
  wire [3:0] bit_extender_5_out, bit_extender_6_out;
  wire [7:0] bit_extender_3_out, bit_extender_4_out, dIn, dOut, shift_register_1_q0, shift_register_1_q1;
  wire [7:4] register_1_q;
  wire [15:0] adder_1_out, bit_extender_1_out, bit_extender_2_out, cs, cu, demultiplexer_1_out0,
       demultiplexer_1_out1, demultiplexer_1_out2, demultiplexer_1_out3, demultiplexer_1_out4,
       demultiplexer_1_out5, demultiplexer_1_out6, demultiplexer_1_out7, demultiplexer_2_out0,
       demultiplexer_2_out1, demultiplexer_2_out2, demultiplexer_2_out3, demultiplexer_2_out4,
       demultiplexer_2_out5, demultiplexer_2_out6, demultiplexer_2_out7, div, div_res, multiplier_1_out, op1,
       op2, register_3_q, register_5_q, rem, res, shifter_1_out, shifter_2_out, subtractor_1_out;

  // Probe on {register_1_q, bits, op}
  // Probe on register_3_q[15:8]
  // Probe on register_3_q[7:0]
  // Probe on register_5_q[15:8]
  // Probe on register_5_q[7:0]
  Counter #(.width(2), .max('h3), .trigger("falling")) counter_1 (
    .Q(counter_1_q), .clk(and_1_out), .clr(decoder_1_out2));  // open: load, D, count, carry
  Decoder #(.select(2), .enable("false")) decoder_1 (
    .out2(decoder_1_out2), .sel(counter_1_q));  // open: out0, out1, out3
  and and_1 (and_1_out, rd_wr_prime, and_3_out);
  and and_2 (Select, IO, comparator_1_eq);
  Comparator #(.width(4), .mode("unsigned")) comparator_1 (
    .a(IO_Address), .b(Device_Address), .eq(comparator_1_eq));  // open: gt, lt
  not not_1 (not_1_out, rd_wr_prime);
  assign bit_extender_1_out = {{8{register_3_q[15]}}, register_3_q[15:8]};  // Bit_Extender bit_extender_1
  Multiplexer #(.width(16), .enable("false")) multiplexer_1 (
    .in0(bit_extender_1_out), .in1(register_3_q), .out(op2), .sel(bits));
  and and_3 (and_3_out, Select, Clock);
  assign bit_extender_2_out = {{8{register_3_q[7]}}, register_3_q[7:0]};  // Bit_Extender bit_extender_2
  Counter #(.width(3), .max('h7)) counter_2 (
    .Q(counter_2_q), .clk(and_3_out), .clr(decoder_1_out2));  // open: load, D, count, carry
  and and_4 (and_4_out, Select, not_1_out);
  Multiplexer #(.width(16), .enable("false")) multiplexer_2 (
    .in0(bit_extender_2_out), .in1(register_5_q), .out(op1), .sel(bits));
  Decoder #(.select(3), .enable("false")) decoder_2 (
    .out3(decoder_2_out3), .out5(decoder_2_out5), .sel(counter_2_q));  // open: out0, out1, out2, out4, out6, out7
  Register register_1 (.D(dIn), .en(and_4_out), .Q({register_1_q, bits, op}), .clk(Clock));  // open: clr
  or or_1 (or_1_out, decoder_2_out3, decoder_2_out5);
  Register register_2 (.D({register_1_q, bits, op}), .en(and_4_out), .Q(register_3_q[15:8]), .clk(Clock));  // open: clr
  Shift_Register #(.width(8), .length(2), .trigger("falling")) shift_register_1 (
    .shift(1'b1), .in({8{1'b0}}), .clk(and_3_out), .out(dOut), .load(or_1_out), .d0(res[15:8]),
    .q0(shift_register_1_q0), .d1(res[7:0]), .q1(shift_register_1_q1));  // open: clr
  // Probe on shift_register_1_q1
  // Probe on shift_register_1_q0
  and and_5 (and_5_out, Select, not_2_out);
  assign dIn = and_5_out ? Data_Bus_In : 8'bz;  // Controlled_Buffer controlled_buffer_1
  assign Data_Bus_Out = and_6_out ? dOut : 8'bz;  // Controlled_Buffer controlled_buffer_2
  and and_6 (and_6_out, rd_wr_prime, Select);
  Register register_3 (.D(register_3_q[15:8]), .en(and_4_out), .Q(register_3_q[7:0]), .clk(Clock));  // open: clr
  not not_2 (not_2_out, rd_wr_prime);
  Bit_Extender #(.in_width(16), .out_width(8)) bit_extender_3 (.in(rem), .out(bit_extender_3_out));
  Register register_4 (.D(register_3_q[7:0]), .en(and_4_out), .Q(register_5_q[15:8]), .clk(Clock));  // open: clr
  Bit_Extender #(.in_width(16), .out_width(8)) bit_extender_4 (.in(div), .out(bit_extender_4_out));
  Register register_5 (.D(register_5_q[15:8]), .en(and_4_out), .Q(register_5_q[7:0]), .clk(Clock));  // open: clr
  Multiplexer #(.width(16), .enable("false")) multiplexer_3 (
    .in0({bit_extender_3_out, bit_extender_4_out}), .in1(div), .out(div_res), .sel(bits));
  Demultiplexer #(.select(3), .width(16), .enable("false")) demultiplexer_1 (
    .out0(demultiplexer_1_out0), .out1(demultiplexer_1_out1), .out2(demultiplexer_1_out2),
    .out3(demultiplexer_1_out3), .out4(demultiplexer_1_out4), .out5(demultiplexer_1_out5),
    .out6(demultiplexer_1_out6), .out7(demultiplexer_1_out7), .in(op1), .sel(op));
  Demultiplexer #(.select(3), .width(16), .enable("false")) demultiplexer_2 (
    .out0(demultiplexer_2_out0), .out1(demultiplexer_2_out1), .out2(demultiplexer_2_out2),
    .out3(demultiplexer_2_out3), .out4(demultiplexer_2_out4), .out5(demultiplexer_2_out5),
    .out6(demultiplexer_2_out6), .out7(demultiplexer_2_out7), .in(op2), .sel(op));
  Bit_Extender #(.in_width(16), .out_width(4)) bit_extender_5 (.in(demultiplexer_2_out6), .out(bit_extender_5_out));
  Bit_Extender #(.in_width(16), .out_width(4)) bit_extender_6 (.in(demultiplexer_2_out7), .out(bit_extender_6_out));
  Multiplexer #(.select(2), .width(16), .enable("false")) multiplexer_4 (
    .in0(16'h1), .in1({16{1'b0}}), .in2({16{1'b1}}), .out(cu), .sel(priority_encoder_2_out));  // open: in3
  Adder #(.width(16)) adder_1 (
    .a(demultiplexer_1_out0), .b(demultiplexer_2_out0), .out(adder_1_out));  // open: cin, cout
  Subtractor #(.width(16)) subtractor_1 (
    .a(demultiplexer_1_out1), .b(demultiplexer_2_out1), .out(subtractor_1_out));  // open: bin, bout
  Multiplier #(.width(16)) multiplier_1 (
    .a(demultiplexer_1_out2), .b(demultiplexer_2_out2), .out(multiplier_1_out));  // open: cin, cout
  Divider #(.width(16)) divider_1 (
    .a(demultiplexer_1_out3), .b(demultiplexer_2_out3), .out(div), .rem(rem));  // open: upper
  Comparator #(.width(16)) comparator_2 (
    .a(demultiplexer_1_out4), .b(demultiplexer_2_out4), .gt(comparator_2_gt), .eq(comparator_2_eq),
    .lt(comparator_2_lt));
  Comparator #(.width(16), .mode("unsigned")) comparator_3 (
    .a(demultiplexer_1_out5), .b(demultiplexer_2_out5), .gt(comparator_3_gt), .eq(comparator_3_eq),
    .lt(comparator_3_lt));
  Shifter #(.width(16)) shifter_1 (.in(demultiplexer_1_out6), .\dist (bit_extender_5_out), .out(shifter_1_out));
  Shifter #(.width(16), .shift("lr")) shifter_2 (
    .in(demultiplexer_1_out7), .\dist (bit_extender_6_out), .out(shifter_2_out));
  Multiplexer #(.select(2), .width(16), .enable("false")) multiplexer_5 (
    .in0(16'h1), .in1({16{1'b0}}), .in2({16{1'b1}}), .out(cs), .sel(priority_encoder_1_out));  // open: in3
  Priority_Encoder #(.select(2)) priority_encoder_1 (
    .in0(comparator_2_gt), .in1(comparator_2_eq), .in2(comparator_2_lt), .out(priority_encoder_1_out));  // open: in3, gs, en_out, en_in
  Priority_Encoder #(.select(2)) priority_encoder_2 (
    .in0(comparator_3_gt), .in1(comparator_3_eq), .in2(comparator_3_lt), .out(priority_encoder_2_out));  // open: in3, gs, en_out, en_in
  Multiplexer #(.select(3), .width(16), .enable("false")) multiplexer_6 (
    .in0(adder_1_out), .in1(subtractor_1_out), .in2(multiplier_1_out), .in3(div_res), .in4(cs), .in5(cu),
    .in6(shifter_1_out), .in7(shifter_2_out), .out(res), .sel(op));
endmodule

module Display_Controller_Mono (
  input  [7:0] Data_Bus_In,
  input  Clock,
  input  rd_wr_prime,
  input  [3:0] IO_Address,
  input  IO,
  input  [3:0] Device_Address,
  input  Fast_Clock,
  output [7:0] Data_Bus_Out,
  output [31:0] Colomn_Scan,
  output [31:0] Data
);

  wire and_1_out, and_5_out, and_7_out, and_9_out, and_10_out, and_13_out, b, b0_clk, b0_str, b1_clk, b1_str,
       b_clr, cmd_clr, cmd_wr, comparator_1_eq, d_ff_1_qn, nor_1_out, not_1_out, not_2_out, not_3_out,
       not_4_out, not_7_out, or_1_out, or_3_out, phase_0, phase_1, phase_2, phase_3, s_r_ff_1_q, Select,
       write;
  wire [1:0] counter_1_q;
  wire [4:0] b0_addr, b1_addr, col, x, y;
  wire [7:0] cmd, dIn, mask, register_2_q, register_3_q;
  wire [31:0] and_8_out, and_11_out, and_12_out, b0_in, b0_out, b1_in, b1_out, b_in, b_out,
       bit_extender_1_out, bit_extender_2_out, bit_extender_3_out, decoder_2_out0, decoder_3_out0,
       multiplexer_1_out, not_6_out, not_8_out, not_9_out, shifter_1_out;

  S_R_Flip_Flop s_r_ff_1 (.Q(s_r_ff_1_q), .preset(write), .reset(or_1_out));  // open: S, clk, R, Qn, en
  Decoder #(.select(2), .disabled(0), .enable("false")) decoder_1 (
    .out0(phase_0), .out1(phase_1), .out2(phase_2), .out3(phase_3), .sel(counter_1_q));
  Counter #(.width(2), .max('h3)) counter_1 (
    .count(s_r_ff_1_q), .Q(counter_1_q), .clk(Fast_Clock), .clr(write));  // open: load, D, carry
  and and_1 (and_1_out, cmd_wr, phase_2);
  assign bit_extender_1_out = {{24{1'b0}}, mask};  // Bit_Extender bit_extender_1
  and and_2 (Select, IO, comparator_1_eq);
  Comparator #(.width(4), .mode("unsigned")) comparator_1 (
    .a(IO_Address), .b(Device_Address), .eq(comparator_1_eq));  // open: gt, lt
  not not_1 (not_1_out, rd_wr_prime);
  and and_3 (cmd_clr, cmd[4], cmd[7]);
  and and_4 (cmd_wr, cmd[5], cmd[7]);
  nor nor_1 (nor_1_out, cmd_clr, cmd_wr);
  or or_1 (or_1_out, phase_3, nor_1_out);
  D_Flip_Flop d_ff_1 (.clk(and_1_out), .D(d_ff_1_qn), .Q(b0_str), .Qn(d_ff_1_qn));  // open: preset, en, reset
  Shifter #(.width(32)) shifter_1 (.in(bit_extender_1_out), .\dist (y), .out(shifter_1_out));
  and and_5 (and_5_out, Select, not_1_out, Clock);
  not not_2 (not_2_out, and_5_out);
  not not_3 (not_3_out, not_2_out);
  and and_6 (write, not_3_out, not_2_out);
  and and_7 (and_7_out, Select, not_1_out);
  Decoder #(.select(5), .disabled(0), .enable("false")) decoder_2 (
    .out0(decoder_2_out0[0]), .out1(decoder_2_out0[1]), .out2(decoder_2_out0[2]), .out3(decoder_2_out0[3]),
    .out4(decoder_2_out0[4]), .out5(decoder_2_out0[5]), .out6(decoder_2_out0[6]), .out7(decoder_2_out0[7]),
    .out8(decoder_2_out0[8]), .out9(decoder_2_out0[9]), .out10(decoder_2_out0[10]),
    .out11(decoder_2_out0[11]), .out12(decoder_2_out0[12]), .out13(decoder_2_out0[13]),
    .out14(decoder_2_out0[14]), .out15(decoder_2_out0[15]), .out16(decoder_2_out0[16]),
    .out17(decoder_2_out0[17]), .out18(decoder_2_out0[18]), .out19(decoder_2_out0[19]),
    .out20(decoder_2_out0[20]), .out21(decoder_2_out0[21]), .out22(decoder_2_out0[22]),
    .out23(decoder_2_out0[23]), .out24(decoder_2_out0[24]), .out25(decoder_2_out0[25]),
    .out26(decoder_2_out0[26]), .out27(decoder_2_out0[27]), .out28(decoder_2_out0[28]),
    .out29(decoder_2_out0[29]), .out30(decoder_2_out0[30]), .out31(decoder_2_out0[31]), .sel(y));
  Register register_1 (.D(dIn), .en(and_7_out), .Q({cmd[7:3], b, cmd[1:0]}), .clk(Clock));  // open: clr
  not not_4 (not_4_out, cmd[0]);
  assign and_8_out = bit_extender_2_out & multiplexer_1_out;  // AND_Gate and_8, 32 bits wide
  Multiplexer #(.width(32), .enable("false")) multiplexer_1 (
    .in0(decoder_2_out0), .in1(shifter_1_out), .out(multiplexer_1_out), .sel(cmd[6]));
  Register register_2 (.D({cmd[7:3], b, cmd[1:0]}), .en(and_7_out), .Q(register_2_q), .clk(Clock));  // open: clr
  not not_5 (b1_str, b0_str);
  assign bit_extender_2_out = {{31{not_4_out}}, not_4_out};  // Bit_Extender bit_extender_2
  assign not_6_out = ~and_8_out;  // NOT_Gate not_6, 32 bits wide
  assign bit_extender_3_out = {{31{cmd[0]}}, cmd[0]};  // Bit_Extender bit_extender_3
  and and_9 (and_9_out, Select, not_7_out);
  assign dIn = and_9_out ? Data_Bus_In : 8'bz;  // Controlled_Buffer controlled_buffer_1
  assign Data_Bus_Out = and_10_out ? register_3_q : 8'bz;  // Controlled_Buffer controlled_buffer_2
  and and_10 (and_10_out, Select, rd_wr_prime);
  Register register_3 (.D(register_2_q), .en(and_7_out), .Q(register_3_q), .clk(Clock));  // open: clr
  assign and_11_out = b_out & not_6_out;  // AND_Gate and_11, 32 bits wide
  assign b_in = and_11_out | and_12_out;  // OR_Gate or_2, 32 bits wide
  assign and_12_out = multiplexer_1_out & bit_extender_3_out;  // AND_Gate and_12, 32 bits wide
  not not_7 (not_7_out, rd_wr_prime);
  or or_3 (or_3_out, phase_1, phase_3);
  and and_13 (and_13_out, or_3_out, cmd_wr);
  Demultiplexer #(.width(32), .enable("false")) demultiplexer_1 (.out0(b1_in), .out1(b0_in), .in(b_in), .sel(b0_str));
  Register register_4 (.D(register_3_q), .en(and_7_out), .Q(mask), .clk(Clock));  // open: clr
  Bit_Extender #(.out_width(5)) bit_extender_4 (.in(register_3_q), .out(x));
  Bit_Extender #(.out_width(5)) bit_extender_5 (.in(register_2_q), .out(y));
  Multiplexer #(.enable("false")) multiplexer_2 (.in0(and_13_out), .in1(1'b0), .out(b1_clk), .sel(b0_str));
  Multiplexer #(.enable("false")) multiplexer_3 (.in0(1'b0), .in1(and_13_out), .out(b0_clk), .sel(b0_str));
  and and_14 (b_clr, cmd_clr, phase_0);
  Multiplexer #(.width(5), .enable("false")) multiplexer_4 (.in0(col), .in1(x), .out(b0_addr), .sel(b0_str));
  Multiplexer #(.width(5), .enable("false")) multiplexer_5 (.in0(x), .in1(col), .out(b1_addr), .sel(b0_str));
  Multiplexer #(.width(32), .enable("false")) multiplexer_6 (.in0(b0_out), .in1(b1_out), .out(Data), .sel(b0_str));
  Multiplexer #(.width(32), .enable("false")) multiplexer_7 (.in0(b1_out), .in1(b0_out), .out(b_out), .sel(b0_str));
  Decoder #(.select(5), .disabled(0), .enable("false")) decoder_3 (
    .out0(decoder_3_out0[0]), .out1(decoder_3_out0[1]), .out2(decoder_3_out0[2]), .out3(decoder_3_out0[3]),
    .out4(decoder_3_out0[4]), .out5(decoder_3_out0[5]), .out6(decoder_3_out0[6]), .out7(decoder_3_out0[7]),
    .out8(decoder_3_out0[8]), .out9(decoder_3_out0[9]), .out10(decoder_3_out0[10]),
    .out11(decoder_3_out0[11]), .out12(decoder_3_out0[12]), .out13(decoder_3_out0[13]),
    .out14(decoder_3_out0[14]), .out15(decoder_3_out0[15]), .out16(decoder_3_out0[16]),
    .out17(decoder_3_out0[17]), .out18(decoder_3_out0[18]), .out19(decoder_3_out0[19]),
    .out20(decoder_3_out0[20]), .out21(decoder_3_out0[21]), .out22(decoder_3_out0[22]),
    .out23(decoder_3_out0[23]), .out24(decoder_3_out0[24]), .out25(decoder_3_out0[25]),
    .out26(decoder_3_out0[26]), .out27(decoder_3_out0[27]), .out28(decoder_3_out0[28]),
    .out29(decoder_3_out0[29]), .out30(decoder_3_out0[30]), .out31(decoder_3_out0[31]), .sel(col));
  Counter #(.width(5), .max('h1f)) counter_2 (.Q(col), .clk(Fast_Clock));  // open: load, D, count, carry, clr
  assign not_8_out = ~decoder_3_out0;  // NOT_Gate not_8, 32 bits wide
  assign not_9_out = ~not_8_out;  // NOT_Gate not_9, 32 bits wide
  assign Colomn_Scan = not_9_out & not_8_out;  // AND_Gate and_15, 32 bits wide
  RAM #(.addrWidth(5), .dataWidth(32), .bus("separate")) ram_1 (
    .addr(b0_addr), .din(b0_in), .data(b0_out), .str(b0_str), .sel(1'b1), .clk(b0_clk), .ld(1'b1), .clr(b_clr));
  RAM #(.addrWidth(5), .dataWidth(32), .bus("separate")) ram_2 (
    .addr(b1_addr), .din(b1_in), .data(b1_out), .str(b1_str), .sel(1'b1), .clk(b1_clk), .ld(1'b1), .clr(b_clr));

  // Other names for the same wires on the sheet: b_sel = b0_str; r = cmd[0]; g = cmd[1]; cmd[2] = b;
  //   cmd_wr_block = cmd[6]; cmd_data_prime = cmd[7]; master_clk = Fast_Clock

  // Notes on the sheet:
  //   Fast_Clock: pull=down
  //   active
endmodule

module Display_Controller_Color (
  input  [7:0] Data_Bus_In,
  input  Clock,
  input  rd_wr_prime,
  input  [3:0] IO_Address,
  input  IO,
  input  [3:0] Device_Address,
  input  Fast_Clock,
  output [7:0] Data_Bus_Out,
  output [31:0] Colomn_Scan_R,
  output [31:0] Data_Red,
  output [31:0] Colomn_Scan_G,
  output [31:0] Colomn_Scan_B,
  output [31:0] Data_Green,
  output [31:0] Data_Blue
);

  wire and_1_out, and_6_out, and_10_out, and_13_out, and_14_out, and_17_out, b, b0_clk, b0_str, b1_clk,
       b1_str, b_clr, cmd_clr, cmd_wr, comparator_1_eq, d_ff_1_qn, nor_1_out, not_1_out, not_2_out,
       not_3_out, not_4_out, not_7_out, not_9_out, not_11_out, or_1_out, or_4_out, phase_0, phase_1, phase_2,
       phase_3, s_r_ff_1_q, Select, write;
  wire [1:0] counter_1_q;
  wire [4:0] b0_addr, b1_addr, col, x, y;
  wire [7:0] cmd, dIn, mask, register_2_q, register_3_q;
  wire [31:0] and_5_out, and_8_out, and_9_out, and_11_out, and_12_out, and_15_out, and_16_out, and_18_out,
       and_19_out, b0b_in, b0b_out, b0g_in, b0g_out, b0r_in, b0r_out, b1b_in, b1b_out, b1g_in, b1g_out,
       b1r_in, b1r_out, bb_in, bb_out, bg_in, bg_out, bit_extender_1_out, bit_extender_2_out,
       bit_extender_3_out, bit_extender_4_out, bit_extender_5_out, bit_extender_6_out, bit_extender_7_out,
       br_in, br_out, decoder_2_out0, decoder_3_out30, decoder_4_out31, decoder_5_out0, multiplexer_1_out,
       not_5_out, not_8_out, not_10_out, not_12_out, not_13_out, not_14_out, not_15_out, not_16_out,
       not_17_out, shifter_1_out;

  S_R_Flip_Flop s_r_ff_1 (.Q(s_r_ff_1_q), .preset(write), .reset(or_1_out));  // open: S, clk, R, Qn, en
  Decoder #(.select(2), .disabled(0), .enable("false")) decoder_1 (
    .out0(phase_0), .out1(phase_1), .out2(phase_2), .out3(phase_3), .sel(counter_1_q));
  Counter #(.width(2), .max('h3)) counter_1 (
    .count(s_r_ff_1_q), .Q(counter_1_q), .clk(Fast_Clock), .clr(write));  // open: load, D, carry
  and and_1 (and_1_out, cmd_wr, phase_2);
  assign bit_extender_1_out = {{24{1'b0}}, mask};  // Bit_Extender bit_extender_1
  and and_2 (Select, IO, comparator_1_eq);
  Comparator #(.width(4), .mode("unsigned")) comparator_1 (
    .a(IO_Address), .b(Device_Address), .eq(comparator_1_eq));  // open: gt, lt
  not not_1 (not_1_out, rd_wr_prime);
  and and_3 (cmd_clr, cmd[4], cmd[7]);
  and and_4 (cmd_wr, cmd[5], cmd[7]);
  nor nor_1 (nor_1_out, cmd_clr, cmd_wr);
  or or_1 (or_1_out, phase_3, nor_1_out);
  D_Flip_Flop d_ff_1 (.clk(and_1_out), .D(d_ff_1_qn), .Q(b0_str), .Qn(d_ff_1_qn));  // open: preset, en, reset
  Shifter #(.width(32)) shifter_1 (.in(bit_extender_1_out), .\dist (y), .out(shifter_1_out));
  not not_2 (not_2_out, cmd[1]);
  assign and_5_out = bit_extender_3_out & multiplexer_1_out;  // AND_Gate and_5, 32 bits wide
  assign bit_extender_2_out = {{31{cmd[1]}}, cmd[1]};  // Bit_Extender bit_extender_2
  and and_6 (and_6_out, Select, not_1_out, Clock);
  not not_3 (not_3_out, and_6_out);
  not not_4 (not_4_out, not_3_out);
  and and_7 (write, not_4_out, not_3_out);
  assign bit_extender_3_out = {{31{not_2_out}}, not_2_out};  // Bit_Extender bit_extender_3
  assign and_8_out = bg_out & not_5_out;  // AND_Gate and_8, 32 bits wide
  assign not_5_out = ~and_5_out;  // NOT_Gate not_5, 32 bits wide
  assign and_9_out = multiplexer_1_out & bit_extender_2_out;  // AND_Gate and_9, 32 bits wide
  Counter #(.width(5), .max('h1f)) counter_2 (.Q(col), .clk(Fast_Clock));  // open: load, D, count, carry, clr
  and and_10 (and_10_out, Select, not_1_out);
  Decoder #(.select(5), .disabled(0), .enable("false")) decoder_2 (
    .out0(decoder_2_out0[0]), .out1(decoder_2_out0[1]), .out2(decoder_2_out0[2]), .out3(decoder_2_out0[3]),
    .out4(decoder_2_out0[4]), .out5(decoder_2_out0[5]), .out6(decoder_2_out0[6]), .out7(decoder_2_out0[7]),
    .out8(decoder_2_out0[8]), .out9(decoder_2_out0[9]), .out10(decoder_2_out0[10]),
    .out11(decoder_2_out0[11]), .out12(decoder_2_out0[12]), .out13(decoder_2_out0[13]),
    .out14(decoder_2_out0[14]), .out15(decoder_2_out0[15]), .out16(decoder_2_out0[16]),
    .out17(decoder_2_out0[17]), .out18(decoder_2_out0[18]), .out19(decoder_2_out0[19]),
    .out20(decoder_2_out0[20]), .out21(decoder_2_out0[21]), .out22(decoder_2_out0[22]),
    .out23(decoder_2_out0[23]), .out24(decoder_2_out0[24]), .out25(decoder_2_out0[25]),
    .out26(decoder_2_out0[26]), .out27(decoder_2_out0[27]), .out28(decoder_2_out0[28]),
    .out29(decoder_2_out0[29]), .out30(decoder_2_out0[30]), .out31(decoder_2_out0[31]), .sel(y));
  assign bg_in = and_8_out | and_9_out;  // OR_Gate or_2, 32 bits wide
  Register register_1 (.D(dIn), .en(and_10_out), .Q({cmd[7:3], b, cmd[1:0]}), .clk(Clock));  // open: clr
  assign and_11_out = bit_extender_4_out & multiplexer_1_out;  // AND_Gate and_11, 32 bits wide
  Multiplexer #(.width(32), .enable("false")) multiplexer_1 (
    .in0(decoder_2_out0), .in1(shifter_1_out), .out(multiplexer_1_out), .sel(cmd[6]));
  Register register_2 (.D({cmd[7:3], b, cmd[1:0]}), .en(and_10_out), .Q(register_2_q), .clk(Clock));  // open: clr
  not not_6 (b1_str, b0_str);
  not not_7 (not_7_out, cmd[0]);
  assign bit_extender_4_out = {{31{not_7_out}}, not_7_out};  // Bit_Extender bit_extender_4
  assign not_8_out = ~and_11_out;  // NOT_Gate not_8, 32 bits wide
  assign bit_extender_5_out = {{31{cmd[0]}}, cmd[0]};  // Bit_Extender bit_extender_5
  assign and_12_out = bit_extender_6_out & multiplexer_1_out;  // AND_Gate and_12, 32 bits wide
  and and_13 (and_13_out, Select, not_11_out);
  assign dIn = and_13_out ? Data_Bus_In : 8'bz;  // Controlled_Buffer controlled_buffer_1
  assign Data_Bus_Out = and_14_out ? mask : 8'bz;  // Controlled_Buffer controlled_buffer_2
  and and_14 (and_14_out, Select, rd_wr_prime);
  Register register_3 (.D(register_2_q), .en(and_10_out), .Q(register_3_q), .clk(Clock));  // open: clr
  assign and_15_out = br_out & not_8_out;  // AND_Gate and_15, 32 bits wide
  assign br_in = and_15_out | and_16_out;  // OR_Gate or_3, 32 bits wide
  assign and_16_out = multiplexer_1_out & bit_extender_5_out;  // AND_Gate and_16, 32 bits wide
  not not_9 (not_9_out, b);
  assign bit_extender_6_out = {{31{not_9_out}}, not_9_out};  // Bit_Extender bit_extender_6
  assign not_10_out = ~and_12_out;  // NOT_Gate not_10, 32 bits wide
  assign bit_extender_7_out = {{31{b}}, b};  // Bit_Extender bit_extender_7
  not not_11 (not_11_out, rd_wr_prime);
  or or_4 (or_4_out, phase_1, phase_3);
  and and_17 (and_17_out, or_4_out, cmd_wr);
  assign and_18_out = bb_out & not_10_out;  // AND_Gate and_18, 32 bits wide
  assign bb_in = and_18_out | and_19_out;  // OR_Gate or_5, 32 bits wide
  assign and_19_out = multiplexer_1_out & bit_extender_7_out;  // AND_Gate and_19, 32 bits wide
  Register register_4 (.D(register_3_q), .en(and_10_out), .Q(mask), .clk(Clock));  // open: clr
  Bit_Extender #(.out_width(5)) bit_extender_8 (.in(register_3_q), .out(x));
  Bit_Extender #(.out_width(5)) bit_extender_9 (.in(register_2_q), .out(y));
  Multiplexer #(.enable("false")) multiplexer_2 (.in0(and_17_out), .in1(1'b0), .out(b1_clk), .sel(b0_str));
  Multiplexer #(.enable("false")) multiplexer_3 (.in0(1'b0), .in1(and_17_out), .out(b0_clk), .sel(b0_str));
  and and_20 (b_clr, cmd_clr, phase_0);
  Multiplexer #(.width(5), .enable("false")) multiplexer_4 (.in0(col), .in1(x), .out(b0_addr), .sel(b0_str));
  Multiplexer #(.width(5), .enable("false")) multiplexer_5 (.in0(x), .in1(col), .out(b1_addr), .sel(b0_str));
  Multiplexer #(.width(32), .enable("false")) multiplexer_6 (
    .in0(b0r_out), .in1(b1r_out), .out(Data_Red), .sel(b0_str));
  Decoder #(.select(5), .disabled(0), .enable("false")) decoder_3 (
    .out0(decoder_3_out30[2]), .out1(decoder_3_out30[3]), .out2(decoder_3_out30[4]),
    .out3(decoder_3_out30[5]), .out4(decoder_3_out30[6]), .out5(decoder_3_out30[7]),
    .out6(decoder_3_out30[8]), .out7(decoder_3_out30[9]), .out8(decoder_3_out30[10]),
    .out9(decoder_3_out30[11]), .out10(decoder_3_out30[12]), .out11(decoder_3_out30[13]),
    .out12(decoder_3_out30[14]), .out13(decoder_3_out30[15]), .out14(decoder_3_out30[16]),
    .out15(decoder_3_out30[17]), .out16(decoder_3_out30[18]), .out17(decoder_3_out30[19]),
    .out18(decoder_3_out30[20]), .out19(decoder_3_out30[21]), .out20(decoder_3_out30[22]),
    .out21(decoder_3_out30[23]), .out22(decoder_3_out30[24]), .out23(decoder_3_out30[25]),
    .out24(decoder_3_out30[26]), .out25(decoder_3_out30[27]), .out26(decoder_3_out30[28]),
    .out27(decoder_3_out30[29]), .out28(decoder_3_out30[30]), .out29(decoder_3_out30[31]),
    .out30(decoder_3_out30[0]), .out31(decoder_3_out30[1]), .sel(col));
  Demultiplexer #(.width(32), .enable("false")) demultiplexer_1 (
    .out0(b1r_in), .out1(b0r_in), .in(br_in), .sel(b0_str));
  Demultiplexer #(.width(32), .enable("false")) demultiplexer_2 (
    .out0(b1g_in), .out1(b0g_in), .in(bg_in), .sel(b0_str));
  Demultiplexer #(.width(32), .enable("false")) demultiplexer_3 (
    .out0(b1b_in), .out1(b0b_in), .in(bb_in), .sel(b0_str));
  Multiplexer #(.width(32), .enable("false")) multiplexer_7 (.in0(b1r_out), .in1(b0r_out), .out(br_out), .sel(b0_str));
  Multiplexer #(.width(32), .enable("false")) multiplexer_8 (.in0(b1g_out), .in1(b0g_out), .out(bg_out), .sel(b0_str));
  Multiplexer #(.width(32), .enable("false")) multiplexer_9 (.in0(b1b_out), .in1(b0b_out), .out(bb_out), .sel(b0_str));
  assign not_12_out = ~decoder_3_out30;  // NOT_Gate not_12, 32 bits wide
  assign not_13_out = ~not_12_out;  // NOT_Gate not_13, 32 bits wide
  assign Colomn_Scan_R = not_12_out & not_13_out;  // AND_Gate and_21, 32 bits wide
  Multiplexer #(.width(32), .enable("false")) multiplexer_10 (
    .in0(b0g_out), .in1(b1g_out), .out(Data_Green), .sel(b0_str));
  Multiplexer #(.width(32), .enable("false")) multiplexer_11 (
    .in0(b0b_out), .in1(b1b_out), .out(Data_Blue), .sel(b0_str));
  Decoder #(.select(5), .disabled(0), .enable("false")) decoder_4 (
    .out0(decoder_4_out31[1]), .out1(decoder_4_out31[2]), .out2(decoder_4_out31[3]),
    .out3(decoder_4_out31[4]), .out4(decoder_4_out31[5]), .out5(decoder_4_out31[6]),
    .out6(decoder_4_out31[7]), .out7(decoder_4_out31[8]), .out8(decoder_4_out31[9]),
    .out9(decoder_4_out31[10]), .out10(decoder_4_out31[11]), .out11(decoder_4_out31[12]),
    .out12(decoder_4_out31[13]), .out13(decoder_4_out31[14]), .out14(decoder_4_out31[15]),
    .out15(decoder_4_out31[16]), .out16(decoder_4_out31[17]), .out17(decoder_4_out31[18]),
    .out18(decoder_4_out31[19]), .out19(decoder_4_out31[20]), .out20(decoder_4_out31[21]),
    .out21(decoder_4_out31[22]), .out22(decoder_4_out31[23]), .out23(decoder_4_out31[24]),
    .out24(decoder_4_out31[25]), .out25(decoder_4_out31[26]), .out26(decoder_4_out31[27]),
    .out27(decoder_4_out31[28]), .out28(decoder_4_out31[29]), .out29(decoder_4_out31[30]),
    .out30(decoder_4_out31[31]), .out31(decoder_4_out31[0]), .sel(col));
  RAM #(.addrWidth(5), .dataWidth(32), .bus("separate")) ram_1 (
    .addr(b0_addr), .din(b0r_in), .data(b0r_out), .str(b0_str), .sel(1'b1), .clk(b0_clk), .ld(1'b1),
    .clr(b_clr));
  RAM #(.addrWidth(5), .dataWidth(32), .bus("separate")) ram_2 (
    .addr(b0_addr), .din(b0g_in), .data(b0g_out), .str(b0_str), .sel(1'b1), .clk(b0_clk), .ld(1'b1),
    .clr(b_clr));
  assign not_14_out = ~decoder_4_out31;  // NOT_Gate not_14, 32 bits wide
  assign not_15_out = ~not_14_out;  // NOT_Gate not_15, 32 bits wide
  RAM #(.addrWidth(5), .dataWidth(32), .bus("separate")) ram_3 (
    .addr(b0_addr), .din(b0b_in), .data(b0b_out), .str(b0_str), .sel(1'b1), .clk(b0_clk), .ld(1'b1),
    .clr(b_clr));
  assign Colomn_Scan_G = not_14_out & not_15_out;  // AND_Gate and_22, 32 bits wide
  Decoder #(.select(5), .disabled(0), .enable("false")) decoder_5 (
    .out0(decoder_5_out0[0]), .out1(decoder_5_out0[1]), .out2(decoder_5_out0[2]), .out3(decoder_5_out0[3]),
    .out4(decoder_5_out0[4]), .out5(decoder_5_out0[5]), .out6(decoder_5_out0[6]), .out7(decoder_5_out0[7]),
    .out8(decoder_5_out0[8]), .out9(decoder_5_out0[9]), .out10(decoder_5_out0[10]),
    .out11(decoder_5_out0[11]), .out12(decoder_5_out0[12]), .out13(decoder_5_out0[13]),
    .out14(decoder_5_out0[14]), .out15(decoder_5_out0[15]), .out16(decoder_5_out0[16]),
    .out17(decoder_5_out0[17]), .out18(decoder_5_out0[18]), .out19(decoder_5_out0[19]),
    .out20(decoder_5_out0[20]), .out21(decoder_5_out0[21]), .out22(decoder_5_out0[22]),
    .out23(decoder_5_out0[23]), .out24(decoder_5_out0[24]), .out25(decoder_5_out0[25]),
    .out26(decoder_5_out0[26]), .out27(decoder_5_out0[27]), .out28(decoder_5_out0[28]),
    .out29(decoder_5_out0[29]), .out30(decoder_5_out0[30]), .out31(decoder_5_out0[31]), .sel(col));
  RAM #(.addrWidth(5), .dataWidth(32), .bus("separate")) ram_4 (
    .addr(b1_addr), .din(b1r_in), .data(b1r_out), .str(b1_str), .sel(1'b1), .clk(b1_clk), .ld(1'b1),
    .clr(b_clr));
  RAM #(.addrWidth(5), .dataWidth(32), .bus("separate")) ram_5 (
    .addr(b1_addr), .din(b1g_in), .data(b1g_out), .str(b1_str), .sel(1'b1), .clk(b1_clk), .ld(1'b1),
    .clr(b_clr));
  assign not_16_out = ~decoder_5_out0;  // NOT_Gate not_16, 32 bits wide
  assign not_17_out = ~not_16_out;  // NOT_Gate not_17, 32 bits wide
  RAM #(.addrWidth(5), .dataWidth(32), .bus("separate")) ram_6 (
    .addr(b1_addr), .din(b1b_in), .data(b1b_out), .str(b1_str), .sel(1'b1), .clk(b1_clk), .ld(1'b1),
    .clr(b_clr));
  assign Colomn_Scan_B = not_16_out & not_17_out;  // AND_Gate and_23, 32 bits wide

  // Other names for the same wires on the sheet: b_sel = b0_str; r = cmd[0]; g = cmd[1]; cmd[2] = b;
  //   cmd_wr_block = cmd[6]; cmd_data_prime = cmd[7]; master_clk = Fast_Clock

  // Notes on the sheet:
  //   Fast_Clock: pull=down
  //   active
endmodule

module Clock_Divider (
  input  [7:0] Divide_Hi,
  input  [7:0] Divide_Lo,
  input  Fast_Clock,
  output Divided_Clock
);

  wire d_ff_1_qn, decoder_1_out0, decoder_1_out1, decoder_1_out2, decoder_1_out3, decoder_1_out4,
       decoder_1_out5, decoder_1_out6, decoder_1_out7, multiplexer_1_out, multiplexer_2_out;
  wire [2:0] counter_2_q, priority_encoder_1_out, priority_encoder_2_out;
  wire [7:0] counter_1_q;

  Counter counter_1 (.Q(counter_1_q), .clk(Fast_Clock), .clr(multiplexer_2_out));  // open: load, D, count, carry
  Multiplexer #(.select(3), .enable("false")) multiplexer_1 (
    .in0(counter_1_q[0]), .in1(counter_1_q[1]), .in2(counter_1_q[2]), .in3(counter_1_q[3]),
    .in4(counter_1_q[4]), .in5(counter_1_q[5]), .in6(counter_1_q[6]), .in7(counter_1_q[7]),
    .out(multiplexer_1_out), .sel(priority_encoder_1_out));
  Priority_Encoder priority_encoder_1 (
    .in0(Divide_Hi[0]), .in1(Divide_Hi[1]), .in2(Divide_Hi[2]), .in3(Divide_Hi[3]), .in4(Divide_Hi[4]),
    .in5(Divide_Hi[5]), .in6(Divide_Hi[6]), .in7(Divide_Hi[7]), .out(priority_encoder_1_out));  // open: en_in, gs, en_out
  Counter #(.width(3), .max('h7)) counter_2 (
    .Q(counter_2_q), .clk(multiplexer_1_out), .clr(multiplexer_2_out));  // open: load, D, count, carry
  Decoder #(.select(3), .enable("false")) decoder_1 (
    .out0(decoder_1_out0), .out1(decoder_1_out1), .out2(decoder_1_out2), .out3(decoder_1_out3),
    .out4(decoder_1_out4), .out5(decoder_1_out5), .out6(decoder_1_out6), .out7(decoder_1_out7),
    .sel(counter_2_q));
  Priority_Encoder priority_encoder_2 (
    .in0(Divide_Lo[0]), .in1(Divide_Lo[1]), .in2(Divide_Lo[2]), .in3(Divide_Lo[3]), .in4(Divide_Lo[4]),
    .in5(Divide_Lo[5]), .in6(Divide_Lo[6]), .in7(Divide_Lo[7]), .out(priority_encoder_2_out));  // open: en_in, gs, en_out
  Multiplexer #(.select(3), .enable("false")) multiplexer_2 (
    .in0(decoder_1_out0), .in1(decoder_1_out1), .in2(decoder_1_out2), .in3(decoder_1_out3),
    .in4(decoder_1_out4), .in5(decoder_1_out5), .in6(decoder_1_out6), .in7(decoder_1_out7),
    .out(multiplexer_2_out), .sel(priority_encoder_2_out));
  D_Flip_Flop d_ff_1 (
    .clk(multiplexer_2_out), .D(d_ff_1_qn), .Q(Divided_Clock), .Qn(d_ff_1_qn));  // open: preset, en, reset

  // Notes on the sheet:
  //   Divide_Lo: pull=up
  //   Divide_Hi: pull=up
endmodule

module RAM_Controller (
  input  Clock,
  input  rd_wr_prime,
  input  [3:0] IO_Address,
  input  IO,
  input  [3:0] Device_Address,
  input  [7:0] Data_Bus_In,
  input  [7:0] Address_Bus,
  output [6:0] RAM_Global_Address,
  output [7:0] Data_Bus_Out,
  output [14:0] RAM_Paged_Address
);

  wire comparator_1_eq, not_1_out, Read, Select, Write;

  Comparator #(.width(4), .mode("unsigned")) comparator_1 (
    .a(IO_Address), .b(Device_Address), .eq(comparator_1_eq));  // open: gt, lt
  assign Data_Bus_Out = Read ? RAM_Paged_Address[14:7] : 8'bz;  // Controlled_Buffer controlled_buffer_1
  and and_1 (Select, IO, comparator_1_eq);
  and and_2 (Write, Select, not_1_out);
  not not_1 (not_1_out, rd_wr_prime);
  and and_3 (Read, rd_wr_prime, Select);
  Register register_1 (.D(Data_Bus_In), .en(Write), .Q(RAM_Paged_Address[14:7]), .clk(Clock));  // open: clr
  Bit_Extender #(.out_width(7)) bit_extender_1 (.in(Address_Bus), .out(RAM_Global_Address));

  assign RAM_Paged_Address[6:0] = RAM_Global_Address;

  // Other names for the same wires on the sheet: Address_Hi[7:0] = RAM_Paged_Address[14:7];
  //   Data_Bus_Out_t[7:0] = RAM_Paged_Address[14:7]
endmodule

module ROM_Controller (
  input  Clock,
  input  rd_wr_prime,
  input  [3:0] IO_Address,
  input  IO,
  input  [3:0] Device_Address,
  input  [7:0] ISR_Bank,
  input  [7:0] Data_Bus_In,
  input  IAck,
  output [7:0] Data_Bus_Out,
  output [7:0] Addrerss_Out,
  output IR_Enable
);

  wire and_2_out, comparator_1_eq, d_ff_1_q, d_ff_2_q, d_ff_3_q, d_ff_4_q, d_ff_6_q, d_ff_7_q, d_ff_9_q, dec,
       decoder_1_out1, decoder_1_out2, decoder_1_out3, front_detector_short_1_out, inc, IR,
       multiplexer_1_out, or_1_out, or_2_out, or_3_out, pop, push, rti, s_r_ff_1_q, Select, store, Write,
       Write_Clock;
  wire [1:0] counter_1_q;
  wire [6:0] multiplexer_2_out;
  wire [7:0] counter_2_q, register_1_q;

  and and_1 (Select, IO, comparator_1_eq);
  Comparator #(.width(4), .mode("unsigned")) comparator_1 (
    .a(IO_Address), .b(Device_Address), .eq(comparator_1_eq));  // open: gt, lt
  assign Data_Bus_Out = and_2_out ? Addrerss_Out : 8'bz;  // Controlled_Buffer controlled_buffer_1
  and and_2 (and_2_out, rd_wr_prime, Select);
  Counter #(.width(2), .max('h3)) counter_1 (
    .count(s_r_ff_1_q), .Q(counter_1_q), .clk(Clock), .clr(or_1_out));  // open: load, D, carry
  S_R_Flip_Flop #(.trigger("falling")) s_r_ff_1 (
    .S(multiplexer_1_out), .clk(Clock), .R(decoder_1_out3), .Q(s_r_ff_1_q), .preset(IAck), .reset(or_1_out));  // open: Qn, en
  or or_1 (or_1_out, d_ff_1_q, dec);
  D_Flip_Flop d_ff_1 (.clk(Clock), .D(1'b0), .Q(d_ff_1_q), .preset(Write_Clock));  // open: Qn, en, reset
  Decoder #(.select(2), .disabled(0), .enable("false")) decoder_1 (
    .out1(decoder_1_out1), .out2(decoder_1_out2), .out3(decoder_1_out3), .sel(counter_1_q));  // open: out0
  Multiplexer #(.enable("false")) multiplexer_1 (.in0(d_ff_2_q), .in1(d_ff_9_q), .out(multiplexer_1_out), .sel(rti));
  D_Flip_Flop d_ff_2 (.clk(Clock), .D(d_ff_1_q), .Q(d_ff_2_q));  // open: Qn, preset, en, reset
  Counter counter_2 (.load(pop), .Q(counter_2_q), .clk(or_2_out));  // open: D, count, carry, clr
  or or_2 (or_2_out, inc, dec);
  Register register_1 (.D(Data_Bus_In), .en(Write), .Q(register_1_q), .clk(Clock));  // open: clr
  Front_Detector_Short front_detector_short_1 (.In(decoder_1_out3), .Out(front_detector_short_1_out));
  D_Flip_Flop d_ff_3 (.clk(Clock), .D(d_ff_2_q), .Q(d_ff_3_q));  // open: Qn, preset, en, reset
  and and_3 (Write, Select, ~rd_wr_prime);  // AND_Gate
  and and_4 (rti, multiplexer_2_out[0], pop);
  and and_5 (dec, decoder_1_out1, pop);
  and and_6 (inc, decoder_1_out2, push);
  and and_7 (store, push, front_detector_short_1_out);
  D_Flip_Flop d_ff_4 (.clk(Clock), .D(d_ff_3_q), .Q(d_ff_4_q));  // open: Qn, preset, en, reset
  Multiplexer #(.width(8), .enable("false")) multiplexer_2 (
    .in0(register_1_q), .in1(ISR_Bank), .out({pop, multiplexer_2_out}), .sel(IR));
  not not_1 (push, pop);
  D_Flip_Flop d_ff_5 (.Q(IR), .preset(IAck), .reset(front_detector_short_1_out));  // open: clk, D, Qn, en
  D_Flip_Flop d_ff_6 (.clk(Clock), .D(d_ff_7_q), .Q(d_ff_6_q));  // open: Qn, preset, en, reset
  D_Flip_Flop d_ff_7 (.clk(Clock), .D(d_ff_4_q), .Q(d_ff_7_q));  // open: Qn, preset, en, reset
  and and_8 (Write_Clock, Select, ~rd_wr_prime, Clock);  // AND_Gate
  D_Flip_Flop d_ff_8 (.Qn(IR_Enable), .preset(Write_Clock), .reset(or_3_out));  // open: clk, D, Q, en
  or or_3 (or_3_out, dec, front_detector_short_1_out);
  D_Flip_Flop d_ff_9 (.clk(Clock), .D(d_ff_6_q), .Q(d_ff_9_q));  // open: Qn, preset, en, reset
  RAM #(.bus("separate")) ram_1 (
    .addr(counter_2_q), .din({pop, multiplexer_2_out}), .data(Addrerss_Out), .str(store), .clk(store));  // open: sel, ld, clr

  // Other names for the same wires on the sheet: dIn[7:0] = Data_Bus_In; dOut[7:0] = Addrerss_Out
endmodule

module Joystick_Controller (
  input  Clock,
  input  rd_wr_prime,
  input  [3:0] IO_Address,
  input  IO,
  input  [3:0] Device_Address,
  input  [3:0] X,
  input  [3:0] Y,
  output [7:0] Data_Bus_Out
);

  wire and_1_out, comparator_1_eq, Select;

  Comparator #(.width(4), .mode("unsigned")) comparator_1 (
    .a(IO_Address), .b(Device_Address), .eq(comparator_1_eq));  // open: gt, lt
  assign Data_Bus_Out = and_1_out ? {Y, X} : 8'bz;  // Controlled_Buffer controlled_buffer_1
  and and_1 (and_1_out, rd_wr_prime, Select);
  and and_2 (Select, IO, comparator_1_eq);

  // Other names for the same wires on the sheet: Data_Bus[7:0] = {Y, X}
endmodule

module Keypad_Controller (
  input  Clock,
  input  rd_wr_prime,
  input  [3:0] IO_Address,
  input  IO,
  input  [3:0] Device_Address,
  input  Button_7,
  input  Button_6,
  input  Button_5,
  input  Button_4,
  input  Button_3,
  input  Button_2,
  input  Button_1,
  input  Button_0,
  output IRQ,
  output [7:0] Data_Bus_Out
);

  wire comparator_1_eq, front_detector_short_1_out, front_detector_short_2_out, front_detector_short_3_out,
       front_detector_short_4_out, front_detector_short_5_out, front_detector_short_6_out,
       front_detector_short_7_out, front_detector_short_8_out, front_detector_short_9_out, n8_or_1_out,
       not_1_out, Read, Select;
  wire [7:0] Data_Bus;

  Comparator #(.width(4), .mode("unsigned")) comparator_1 (
    .a(IO_Address), .b(Device_Address), .eq(comparator_1_eq));  // open: gt, lt
  assign Data_Bus_Out = Read ? Data_Bus : 8'bz;  // Controlled_Buffer controlled_buffer_1
  and and_1 (Select, IO, comparator_1_eq);
  and and_2 (Read, rd_wr_prime, Select);
  not not_1 (not_1_out, Read);
  Front_Detector_Short front_detector_short_1 (.In(not_1_out), .Out(front_detector_short_1_out));
  D_Flip_Flop d_ff_1 (
    .Q(Data_Bus[7]), .preset(front_detector_short_2_out), .reset(front_detector_short_1_out));  // open: clk, D, Qn, en
  Front_Detector_Short front_detector_short_2 (.In(Button_7), .Out(front_detector_short_2_out));
  D_Flip_Flop d_ff_2 (
    .Q(Data_Bus[6]), .preset(front_detector_short_3_out), .reset(front_detector_short_1_out));  // open: clk, D, Qn, en
  Front_Detector_Short front_detector_short_3 (.In(Button_6), .Out(front_detector_short_3_out));
  D_Flip_Flop d_ff_3 (
    .Q(Data_Bus[5]), .preset(front_detector_short_4_out), .reset(front_detector_short_1_out));  // open: clk, D, Qn, en
  Front_Detector_Short front_detector_short_4 (.In(Button_5), .Out(front_detector_short_4_out));
  Front_Detector_Short front_detector_short_5 (.In(Button_4), .Out(front_detector_short_5_out));
  D_Flip_Flop d_ff_4 (
    .Q(Data_Bus[3]), .preset(front_detector_short_6_out), .reset(front_detector_short_1_out));  // open: clk, D, Qn, en
  D_Flip_Flop d_ff_5 (
    .Q(Data_Bus[4]), .preset(front_detector_short_5_out), .reset(front_detector_short_1_out));  // open: clk, D, Qn, en
  Front_Detector_Short front_detector_short_6 (.In(Button_3), .Out(front_detector_short_6_out));
  D_Flip_Flop d_ff_6 (
    .Q(Data_Bus[2]), .preset(front_detector_short_7_out), .reset(front_detector_short_1_out));  // open: clk, D, Qn, en
  Front_Detector_Short front_detector_short_7 (.In(Button_2), .Out(front_detector_short_7_out));
  _8_OR u_8_or_1 (
    .Out(n8_or_1_out), .In1(Data_Bus[7]), .In2(Data_Bus[6]), .In3(Data_Bus[5]), .In4(Data_Bus[4]),
    .In5(Data_Bus[3]), .In6(Data_Bus[2]), .In7(Data_Bus[1]), .In8(Data_Bus[0]));
  D_Flip_Flop d_ff_7 (
    .Q(Data_Bus[1]), .preset(front_detector_short_9_out), .reset(front_detector_short_1_out));  // open: clk, D, Qn, en
  Front_Detector_Short front_detector_short_8 (.In(Button_0), .Out(front_detector_short_8_out));
  Front_Detector_Short front_detector_short_9 (.In(Button_1), .Out(front_detector_short_9_out));
  Front_Detector_Short front_detector_short_10 (.In(n8_or_1_out), .Out(IRQ));
  D_Flip_Flop d_ff_8 (
    .Q(Data_Bus[0]), .preset(front_detector_short_8_out), .reset(front_detector_short_1_out));  // open: clk, D, Qn, en

  // Notes on the sheet:
  //   Button_2: pull=down
  //   Button_7: pull=down
  //   Button_5: pull=down
  //   Button_1: pull=down
  //   Button_3: pull=down
  //   Button_6: pull=down
  //   Button_4: pull=down
  //   Button_0: pull=down
endmodule

module Terminal_Controller (
  input  Clock,
  input  rd_wr_prime,
  input  [3:0] IO_Address,
  input  IO,
  input  [3:0] Device_Address,
  input  [6:0] Keyboard_Data,
  input  Keyboard_Available,
  input  [7:0] Data_Bus_In,
  output [6:0] Terminal_Data,
  output Terminal_Clear,
  output Terminal_Clock,
  output Terminal_Enable,
  output Keyboard_Enable,
  output Keyboard_Clock,
  output IRQ,
  output [7:0] Data_Bus_Out
);

  wire comparator_1_eq, not_1_out, Select;
  wire [7:7] Data_Bus_Out_t;

  Comparator #(.width(4), .mode("unsigned")) comparator_1 (
    .a(IO_Address), .b(Device_Address), .eq(comparator_1_eq));  // open: gt, lt
  assign Data_Bus_Out = Keyboard_Enable ? {Data_Bus_Out_t[7], Keyboard_Data} : 8'bz;  // Controlled_Buffer controlled_buffer_1
  and and_1 (Select, IO, comparator_1_eq);
  and and_2 (Terminal_Enable, Select, not_1_out);
  not not_1 (not_1_out, rd_wr_prime);
  and and_3 (Keyboard_Enable, rd_wr_prime, Select);
  not not_2 (Keyboard_Clock, Clock);
  Front_Detector_Short front_detector_short_1 (.In(Keyboard_Available), .Out(IRQ));
  not not_3 (Data_Bus_Out_t[7], Keyboard_Available);

  assign Terminal_Clear = Data_Bus_In[7];
  assign Terminal_Clock = Clock;
  assign Terminal_Data = Data_Bus_In[6:0];

  // Other names for the same wires on the sheet: Data_Bus_Out_t[6:0] = Keyboard_Data; Read = Keyboard_Enable;
  //   Write = Terminal_Enable
endmodule

module Peripheral_Example (
  input  Clock,
  input  rd_wr_prime,
  input  [3:0] IO_Address,
  input  IO,
  input  [3:0] Device_Address,
  input  [7:0] Data_Bus_In,
  output [7:0] Data_Bus_Out
);

  wire comparator_1_eq, not_1_out, Select;
  wire [7:0] Data_Bus;

  Comparator #(.width(4), .mode("unsigned")) comparator_1 (
    .a(IO_Address), .b(Device_Address), .eq(comparator_1_eq));  // open: gt, lt
  assign Data_Bus = not_1_out ? Data_Bus_In : 8'bz;  // Controlled_Buffer controlled_buffer_1
  assign Data_Bus_Out = rd_wr_prime ? Data_Bus : 8'bz;  // Controlled_Buffer controlled_buffer_2
  and and_1 (Select, IO, comparator_1_eq);
  not not_1 (not_1_out, rd_wr_prime);
endmodule
