// Logisim project cdm-platform.circ as structural Verilog: 1 circuit, main circuit Main
module Main (
);

  wire cdm_8_mark5_1_data_inst, Clock, Data, DOWN, HIT, I_O, IAck, Inst, IR_Enable,
       ir_enable_buffer_1_int0_2, ir_enable_buffer_1_int1_2, ir_enable_buffer_1_int2_2,
       ir_enable_buffer_1_int3_2, ir_enable_buffer_1_int4_2, ir_enable_buffer_1_int5_2,
       ir_enable_buffer_1_int6_2, ir_enable_buffer_1_int7_2, irarb_1_ia0, irarb_1_ia1, irarb_1_ia2,
       irarb_1_ia3, irarb_1_ia4, irarb_1_ia5, irarb_1_ia6, irarb_1_ia7, IRQ, kA, kC, kE, LEFT, mem,
       not_1_out, RAM, rd_wr_prime, RIGHT, ROM, tCk, tCr, tE, UP, Vector;
  wire [2:0] vec;
  wire [3:0] I_O_Address;
  wire [6:0] kD, tD;
  wire [7:0] Address_Bus, cdm_8_mark5_1_data_out, controlled_buffer_1_out, Data_Bus, io_reg_1_data_out, PC,
       PS, R0, R1, R2, R3, ROM_Address_Hi, SP;
  wire [11:0] RAM_Address;
  wire [31:0] display_controller_color_1_colomn_scan_b, display_controller_color_1_colomn_scan_g,
       display_controller_color_1_colomn_scan_r, display_controller_color_1_data_blue,
       display_controller_color_1_data_green, display_controller_color_1_data_red,
       display_controller_color_2_colomn_scan_b, display_controller_color_2_colomn_scan_g,
       display_controller_color_2_colomn_scan_r, display_controller_color_2_data_blue,
       display_controller_color_2_data_green, display_controller_color_2_data_red;

  Clock clock_1 (.out(Clock));
  IrArb irarb_1 (
    .IAck(IAck), .Vector(vec), .IRQ(IRQ), .INT0(ir_enable_buffer_1_int0_2), .IA0(irarb_1_ia0),
    .INT1(ir_enable_buffer_1_int1_2), .IA1(irarb_1_ia1), .INT2(ir_enable_buffer_1_int2_2), .IA2(irarb_1_ia2),
    .INT3(ir_enable_buffer_1_int3_2), .IA3(irarb_1_ia3), .INT4(ir_enable_buffer_1_int4_2), .IA4(irarb_1_ia4),
    .INT5(ir_enable_buffer_1_int5_2), .IA5(irarb_1_ia5), .INT6(ir_enable_buffer_1_int6_2), .IA6(irarb_1_ia6),
    .INT7(ir_enable_buffer_1_int7_2), .IA7(irarb_1_ia7));
  Ir_Enable_Buffer ir_enable_buffer_1 (
    .Data_Bus_In(Data_Bus), .rd_wr_prime(rd_wr_prime), .IO_Address(I_O_Address), .IO(I_O),
    .Device_Address(4'b0000), .Clock(Clock), .Data_Bus_Out(Data_Bus), .INT0(UP), .INT1(DOWN), .INT2(LEFT),
    .INT3(RIGHT), .INT4(HIT), .INT0_2(ir_enable_buffer_1_int0_2), .IA0(irarb_1_ia0),
    .INT1_2(ir_enable_buffer_1_int1_2), .IA1(irarb_1_ia1), .INT2_2(ir_enable_buffer_1_int2_2),
    .IA2(irarb_1_ia2), .INT3_2(ir_enable_buffer_1_int3_2), .IA3(irarb_1_ia3),
    .INT4_2(ir_enable_buffer_1_int4_2), .IA4(irarb_1_ia4), .INT5_2(ir_enable_buffer_1_int5_2),
    .IA5(irarb_1_ia5), .INT6_2(ir_enable_buffer_1_int6_2), .IA6(irarb_1_ia6),
    .INT7_2(ir_enable_buffer_1_int7_2), .IA7(irarb_1_ia7), .Enable(IR_Enable));  // open: IA0_2, IA1_2, IA2_2, IA3_2, IA4_2, INT5, IA5_2, INT6, IA6_2, INT7, IA7_2
  Terminal_Controller terminal_controller_1 (
    .Clock(Clock), .rd_wr_prime(rd_wr_prime), .IO_Address(I_O_Address), .IO(I_O), .Keyboard_Enable(kE),
    .Device_Address(4'b0100), .Keyboard_Clock(kC), .Keyboard_Data(kD), .Keyboard_Available(kA),
    .Data_Bus_In(Data_Bus), .Data_Bus_Out(Data_Bus), .Terminal_Data(tD), .Terminal_Clear(tCr),
    .Terminal_Clock(tCk), .Terminal_Enable(tE));  // open: IRQ
  RAM #(.addrWidth(12)) ram_1 (
    .addr(RAM_Address), .data(Data_Bus), .sel(RAM), .clk(Clock), .ld(rd_wr_prime));  // open: clr
  IO_Random_Number_Generator io_random_number_generator_1 (
    .Clock(Clock), .rd_wr_prime(rd_wr_prime), .IO_Address(I_O_Address), .IO(I_O), .Device_Address(4'b0001),
    .Data_Bus_Out(Data_Bus));
  RAM_Controller ram_controller_1 (
    .Clock(Clock), .rd_wr_prime(rd_wr_prime), .IO_Address(I_O_Address), .IO(I_O), .Device_Address(4'b1110),
    .Data_Bus_In(Data_Bus), .Data_Bus_Out(Data_Bus), .Address_Bus(Address_Bus), .RAM_Address(RAM_Address));
  CdM_8_mark5 cdm_8_mark5_1 (
    .clock(Clock), .addr(Address_Bus), .mem_read(rd_wr_prime), .mem_cycle(mem),
    .data_inst(cdm_8_mark5_1_data_inst), .data_out(cdm_8_mark5_1_data_out),
    .data_in(controlled_buffer_1_out), .r0(R0), .r1(R1), .r2(R2), .r3(R3), .PC(PC), .SP(SP), .PS(PS),
    .IAck(IAck), .IRQ(IRQ), .vec(vec));
  assign controlled_buffer_1_out = rd_wr_prime ? Data_Bus : 8'bz;  // Controlled_Buffer controlled_buffer_1
  Address_Decoder address_decoder_1 (
    .data_ins_prime(cdm_8_mark5_1_data_inst), .memory(mem), .Address_Bus(Address_Bus), .Inst(Inst),
    .Data(Data), .Vector(Vector), .I_O(I_O), .ROM(ROM), .I_O_Address(I_O_Address), .RAM(RAM),
    .I_O_Offset(4'b0111));
  assign Data_Bus = not_1_out ? cdm_8_mark5_1_data_out : 8'bz;  // Controlled_Buffer controlled_buffer_2
  not not_1 (not_1_out, rd_wr_prime);
  ROM #(.addrWidth(15)) rom_1 (.addr({ROM_Address_Hi[6:0], Address_Bus}), .data(Data_Bus), .sel(ROM));
  IO_Reg io_reg_1 (
    .Data_Bus_In(Data_Bus), .rd_wr_prime(rd_wr_prime), .IO_Address(I_O_Address), .IO(I_O),
    .Device_Address(4'b0010), .Clock(Clock), .Data_Bus_Out(Data_Bus), .Data_Out(io_reg_1_data_out));
  ROM_Controller rom_controller_1 (
    .Clock(Clock), .rd_wr_prime(rd_wr_prime), .IO_Address(I_O_Address), .IO(I_O), .Device_Address(4'b1000),
    .ISR_Bank(io_reg_1_data_out), .Data_Bus_In(Data_Bus), .Data_Bus_Out(Data_Bus),
    .Addrerss_Out(ROM_Address_Hi), .IAck(IAck), .IR_Enable(IR_Enable));
  Display_Controller_Color display_controller_color_1 (
    .Data_Bus_In(Data_Bus), .Data_Bus_Out(Data_Bus), .Clock(Clock), .rd_wr_prime(rd_wr_prime),
    .IO_Address(I_O_Address), .IO(I_O), .Device_Address(4'b1010), .Fast_Clock(Clock),
    .Data_Red(display_controller_color_1_data_red), .Data_Green(display_controller_color_1_data_green),
    .Colomn_Scan_R(display_controller_color_1_colomn_scan_r),
    .Data_Blue(display_controller_color_1_data_blue),
    .Colomn_Scan_G(display_controller_color_1_colomn_scan_g),
    .Colomn_Scan_B(display_controller_color_1_colomn_scan_b));
  // DotMatrix #(.inputtype("select"), .matrixcols(32), .matrixrows(32), .persist(64)) dotmatrix_1: pin names not known; wires that end beside it: display_controller_color_1_colomn_scan_r, display_controller_color_1_data_red
  // DotMatrix #(.inputtype("select"), .matrixcols(32), .matrixrows(32), .persist(64)) dotmatrix_2: pin names not known; wires that end beside it: display_controller_color_1_colomn_scan_b, display_controller_color_1_data_blue
  // DotMatrix #(.inputtype("select"), .matrixcols(32), .matrixrows(32), .persist(64)) dotmatrix_3: pin names not known; wires that end beside it: display_controller_color_1_colomn_scan_g, display_controller_color_1_data_green
  TTY tty_1 (.data(tD), .clk(tCk), .we(tE), .clr(tCr));
  Keyboard keyboard_1 (.clk(kC), .re(kE), .avail(kA), .data(kD));  // open: clr
  Display_Controller_Color display_controller_color_2 (
    .Data_Bus_In(Data_Bus), .Data_Bus_Out(Data_Bus), .Clock(Clock), .rd_wr_prime(rd_wr_prime),
    .IO_Address(I_O_Address), .IO(I_O), .Device_Address(4'b1011), .Fast_Clock(Clock),
    .Data_Red(display_controller_color_2_data_red), .Data_Green(display_controller_color_2_data_green),
    .Colomn_Scan_R(display_controller_color_2_colomn_scan_r),
    .Data_Blue(display_controller_color_2_data_blue),
    .Colomn_Scan_G(display_controller_color_2_colomn_scan_g),
    .Colomn_Scan_B(display_controller_color_2_colomn_scan_b));
  // DotMatrix #(.inputtype("select"), .matrixcols(32), .matrixrows(32), .persist(64)) dotmatrix_4: pin names not known; wires that end beside it: display_controller_color_2_colomn_scan_r, display_controller_color_2_data_red
  // DotMatrix #(.inputtype("select"), .matrixcols(32), .matrixrows(32), .persist(64)) dotmatrix_5: pin names not known; wires that end beside it: display_controller_color_2_colomn_scan_b, display_controller_color_2_data_blue
  // DotMatrix #(.inputtype("select"), .matrixcols(32), .matrixrows(32), .persist(64)) dotmatrix_6: pin names not known; wires that end beside it: display_controller_color_2_colomn_scan_g, display_controller_color_2_data_green
  Button button_1 (.out(LEFT));
  Button button_2 (.out(UP));
  Button button_3 (.out(DOWN));
  Button button_4 (.out(RIGHT));
  Button button_5 (.out(HIT));
  // Probe on R0
  // Probe on R0
  // Probe on R1
  // Probe on R1
  // Probe on R2
  // Probe on R2
  // Probe on R3
  // Probe on R3
  // Probe on R0
  // Probe on R0
  // Probe on R1
  // Probe on R1
  // Probe on R2
  // Probe on R2
  // Probe on R3
  // Probe on R3
  // Probe on PC
  // Probe on PC
  // Probe on SP
  // Probe on SP
  // Probe on PC
  // Probe on SP
  // Probe on PS

  // Notes on the sheet:
  //   Interrupts
  //   RAM
  //   IO Bus
  //   ROM
  //   contents of rom_1 (hex, n*v repeats v):
  //   cc 70 c1 d1 a c1 d1 80 c1 d9 c5 d0 70 d1 0 a1 d0 43 d6 7b d2 74 d3 a ab d0 61 d6 7b d2 74 d3 a ab d1
  //   a d2 74 bb f e4 40 ab 77 e1 3d d0 0 b0 d3 30 33 ce d0 78 a3 d6 0 cf ee 40 d0 0 a3 ee 26 d4 65 6e 74
  //   65 72 20 32 20 74 6f 20 72 75 6e 20 73 61 6d 70 6c 65 20 70 72 6f 67 72 61 6d 0 65 6e 74 65 72 20 34
  //   20 74 6f 20 72 75 6e 20 62 61 74 74 6c 65 73 68 69 70 0 d2 74 f3 ab 8c f e1 7d d7 124*0 cc 1 c6 c7
  //   cc fd c3 c2 cc 2 c7 cc 2 c3 cc fc c7 c6 cc 2 ee 2d 23*0 c2 c3 d2 d0 19 6 19 19 d2 70 19 f6 a2 c7 c6
  //   a3 a2 d2 e7 a2 d6 47 d6 47 ee 58 8d f6 a2 b2 8e a2 b2 a2 b2 a2 d7 d2 78 d3 80 ab d7 d2 78 d3 80 ab
  //   d7 18*0 1f 11 1f 9 1f 1 17 15 1d 15 15 1f 1c 4 1f 1d 15 17 1f 15 17 10 10 1f 1f 15 1f 1d 15 1f 0 a 0
  //   1 a 0 4 a 0 a a a 0 a 4 10 15 1c 4 a 6 f 12 f 1f 15 a 1f 11 11 1f 11 e 1f 15 11 1f 14 10 f 11 12 1f
  //   4 1f 11 1f 11 11 1f 10 1f 4 1b 1f 1 1 1f 8 1f 1f e 1f e 11 e 1f 14 8 c 12 d 1f 14 b 9 15 12 10 1f 10
  //   1e 1 1e 1c 3 1c 1f 2 1f 1b 4 1b 18 7 18 13 15 19 15*0 d0 50 d6 f d2 74 d3 a ab d2 78 d3 80 ab d7 d2
  //   74 f3 ab 8c f e1 11 d7 56*0 48 65 6c 6c 6f 20 77 6f 72 6c 64 21 164*0 ce d6 c9 d2 0 b8 8e b9 d3 1c
  //   7d e1 18 d2 5 bb d1 5a 17 ab d1 1 ee 24 8d 8d 8d d2 5 bb c0 d0 f6 13 ab c4 d2 1 a9 d2 7b a8 a9 d3 a7
  //   ab ee c2 ce d6 c9 d2 0 b8 8e b9 d3 1 7d e1 48 d2 5 bb d1 a6 17 ab d1 1c ee 54 89 89 89 d2 5 bb c0 d0
  //   a 13 ab c4 d2 1 a9 d2 7b a8 a9 d3 a7 ab ee c2 ce d6 c9 d2 0 b8 8e b9 d3 1 7c e1 78 d2 5 bb d0 9 13
  //   ab d0 1c ee 80 88 88 88 d2 5 bb 8b ab d2 0 a8 d2 7b a8 a9 d3 a7 ab ee c2 ce d6 c9 d2 0 b8 8e b9 8a
  //   d3 1c 7c e1 a5 d2 5 bb d0 f7 13 ab d0 1 ee ad 8c 8c 8c d2 5 bb 8f ab d2 0 a8 d2 7b a8 a9 d3 a7 ab ee
  //   c2 ce d2 6 d3 5 bf ab ee c2 d2 78 d3 81 ab cf d9 d2 0 b8 8e b9 d2 7b a8 a9 d3 a0 ab d7 28*0 30 0 60
  //   0 8c 0 b9 7*0 d2 74 d3 80 ab d0 94 d6 bc d2 74 d3 a ab d2 7a d3 90 ab d2 7b d3 90 ab d2 72 d3 78 bf
  //   8b ab d2 78 bb c2 d2 e 1b c6 ab d6 0 d3 1 d1 0 a7 8d a7 d2 5 d3 da ab d2 71 b8 d1 f 44 d1 0 d2 78 d3
  //   64 13 ab d6 0 d2 71 b8 d1 f 44 d1 1 d2 78 d3 64 13 ab d6 0 d0 1 d2 78 bb c2 d2 1 1b c6 ab d6 0 d2 7b
  //   d3 90 ab d2 7b d0 0 b0 d1 1 b5 d3 a7 a8 a9 ab d2 74 d3 80 ab d2 78 bb c2 d2 2 1b c6 ab d6 0 d0 ae d6
  //   bc d2 74 d3 a ab d2 78 d3 80 ab d7 4c 6f 61 64 69 6e 67 2e 2e 2e 20 50 6c 65 61 73 65 20 77 61 69 74
  //   2e 2e 2e 0 47 61 6d 65 20 66 69 6e 69 73 68 65 64 0 d2 74 f3 ab 8c f e1 be d7 59*0 d2 7e a8 d2 89 d0
  //   1b d1 1b bb f e0 11 c2 d6 33 c6 8a 88 88 88 ea 28 c2 d2 74 d3 2e ab c6 d0 1b 89 89 89 c1 d1 14 16 c5
  //   5 e4 2d ee 9 d2 78 d3 80 ab d7 d2 7a d3 7 ab a8 a9 d3 e2 ab 8c d3 5 ab a8 a9 d3 e2 ab 8c d3 7 ab a8
  //   a9 d3 e2 ab 88 88 d7 174*0 d2 2 d3 14 ab 8e ab d2 71 bb d0 1 43 f e1 23 d6 84 d2 78 bb c2 d2 1 1b c6
  //   ab d6 0 d6 92 d3 1 ee 38 d6 7d d6 71 d2 78 bb c2 d2 6 1b c6 ab d6 0 d6 77 d6 8b d3 0 d2 2 b8 8e b9 5
  //   e0 45 0 e0 45 ee d 0 e1 55 d2 78 bb c2 d2 a 1b c6 ab d6 0 ee 6b d2 78 bb c2 d2 b 1b c6 ab d6 0 d2 78
  //   bb c2 d2 d 1b c6 ab d6 0 d2 78 d3 80 ab d7 d2 70 d3 1f ab d7 d2 70 d3 0 ab d7 d2 7b d3 a7 d6 99 d7
  //   d2 7a d3 a7 d6 99 d7 d2 7b d3 a0 d6 99 d7 d2 7a d3 a0 d6 99 d7 d0 d d1 1f d6 a9 8c d6 a9 8c d6 a9 8c
  //   d6 a9 d7 a8 a9 ab d7 83*0 d2 7e d1 1 a9 d2 4 d1 7a a9 d0 ea b0 0 e1 37 d2 78 bb c2 d2 1 1b c6 ab d6
  //   0 d0 ea b0 d3 1 7c e1 31 d3 e8 bf 73 e1 2d ee ab ee 2f ee 3a ee 37 d2 78 d3 80 ab d7 88 e1 61 d2 78
  //   bb c2 d2 2 1b c6 ab d6 0 d0 ea b0 d3 2 7c e1 5b d3 e8 bf 73 e1 57 ee ab ee 59 ee 64 ee 61 d2 78 d3
  //   80 ab d7 88 e1 8b d2 78 bb c2 d2 3 1b c6 ab d6 0 d0 ea b0 d3 3 7c e1 85 d3 e8 bf 73 e1 81 ee ab ee
  //   83 ee 8e ee 8b d2 78 d3 80 ab d7 88 e1 ab d2 78 bb c2 d2 4 1b c6 ab d6 0 d0 ea b0 d3 4 7c e1 a5 ee
  //   ab ee ab d2 78 d3 80 ab d7 d6 cf d2 78 bb c2 d2 6 1b c6 ab d6 0 d6 cf d0 ea d1 0 a1 d2 3 ba a e0 c9
  //   ee a ee cf d2 78 d3 80 ab d7 d2 0 d3 8 b8 bd a9 ac d2 1 d3 9 b8 bd a9 ac d2 5 d3 a b8 bd a9 ac d7
  //   24*0 d2 71 b8 b9 d3 1f 4c 4d d3 a 73 eb 11 3c 84 ee a 77 eb 18 3d 85 ee 11 c1 d3 9 3d d2 80 d3 a 89
  //   eb 26 1e ee 20 12 c5 bb 97 e3 2e ee 0 7 1d 1d 8d 3 1c 1c 8c d3 f0 ac d3 f4 ad bb 9b e2 4d d3 80 ab
  //   d3 e4 d6 72 d2 78 d3 80 ab d7 d3 3 bc 88 ac d3 ea d0 1 ac d3 eb d0 ec ac a2 b8 d3 81 ab 4*98 d3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
  //   User Area
endmodule
